// Logisim project 实验文件.circ as structural Verilog: 24 circuits, main circuit 七段显示译码器
module \七段显示译码器  (
  input  X3,
  input  X2,
  input  X1,
  input  X0,
  output Seg_1,
  output Seg_2,
  output Seg_3,
  output Seg_4,
  output Seg_5,
  output Seg_6,
  output Seg_7
);

  wire and_1_out, and_2_out, and_3_out, and_4_out, and_5_out, and_6_out, and_7_out, and_8_out, and_9_out,
       and_10_out, and_11_out, and_12_out, and_13_out, and_14_out, and_15_out, and_16_out, not_1_out,
       not_2_out, not_3_out, not_4_out, not_5_out, not_6_out, not_7_out, not_8_out, not_9_out, not_10_out,
       not_11_out, not_12_out, not_13_out, not_14_out, not_15_out, not_16_out, not_17_out, not_18_out,
       not_19_out, not_20_out, not_21_out;

  not not_1 (not_1_out, X2);
  and and_1 (and_1_out, not_1_out, X1);
  and and_2 (and_2_out, X2, not_2_out);
  not not_2 (not_2_out, X1);
  and and_3 (and_3_out, X2, not_3_out);
  not not_3 (not_3_out, X0);
  not not_4 (not_4_out, X1);
  and and_4 (and_4_out, not_4_out, not_5_out);
  not not_5 (not_5_out, X0);
  and and_5 (and_5_out, X2, not_6_out);
  not not_6 (not_6_out, X1);
  and and_6 (and_6_out, X2, not_7_out);
  not not_7 (not_7_out, X0);
  not not_8 (not_8_out, X2);
  and and_7 (and_7_out, not_8_out, not_9_out);
  not not_9 (not_9_out, X0);
  and and_8 (and_8_out, X2, X0);
  not not_10 (not_10_out, X2);
  not not_11 (not_11_out, X1);
  and and_9 (and_9_out, not_11_out, not_12_out);
  not not_12 (not_12_out, X0);
  and and_10 (and_10_out, X1, X0);
  not not_13 (not_13_out, X2);
  and and_11 (and_11_out, not_13_out, not_14_out);
  not not_14 (not_14_out, X0);
  and and_12 (and_12_out, X1, not_15_out);
  not not_15 (not_15_out, X0);
  not not_16 (not_16_out, X2);
  and and_13 (and_13_out, not_16_out, not_17_out);
  not not_17 (not_17_out, X0);
  not not_18 (not_18_out, X2);
  and and_14 (and_14_out, not_18_out, X1);
  and and_15 (and_15_out, X1, not_19_out);
  not not_19 (not_19_out, X0);
  not not_20 (not_20_out, X1);
  and and_16 (and_16_out, X2, not_20_out, X0);
  not not_21 (not_21_out, X1);
  or or_1 (Seg_7, not_21_out, X0, X2);
  or or_2 (Seg_1, and_1_out, and_2_out, and_3_out, X3);
  or or_3 (Seg_2, and_4_out, and_5_out, and_6_out, X3);
  or or_4 (Seg_3, and_7_out, X1, and_8_out, X3);
  or or_5 (Seg_4, not_10_out, and_9_out, and_10_out);
  or or_6 (Seg_5, and_11_out, and_12_out);
  or or_7 (Seg_6, and_13_out, and_14_out, and_15_out, and_16_out, X3);
endmodule

module \七段显示译码器驱动测试  (
);

  wire and_1_out, CLK, d_ff_1_q, d_ff_1_qn, Equal, halt, NEQ, nHalt;
  wire [3:0] Input, input1;
  wire [6:0] Out, Out1, OutS;
  wire [9:0] counter_2_q;
  wire [15:0] multiplexer_1_out, multiplexer_1_out_2, tunnel;

  // Probe on tunnel
  // Probe on 16'hf
  // Probe on tunnel
  Comparator #(.width(16), .mode("twosComplement")) comparator_1 (.a(tunnel), .b(16'hf), .eq(halt));  // open: gt, lt
  RAM #(.addrWidth(16), .dataWidth(4), .bus("separate"), .Select("low")) ram_1 (
    .addr(tunnel), .din(input1), .clk(CLK));  // open: data, str, sel, ld, clr
  not not_1 (nHalt, halt);
  RAM #(.addrWidth(16), .dataWidth(7), .bus("separate"), .Select("low")) ram_2 (
    .addr(tunnel), .din(Out1), .clk(CLK));  // open: data, str, sel, ld, clr
  Counter #(.width(4), .max('hf), .ongoal("wrap"), .trigger("rising"), .behavior("old")) counter_1 (
    .Q(input1), .clk(CLK));  // open: load, D, count, carry, clr, preset
  LED #(.active("true")) \u_测试完成  (.in(halt));
  Counter #(.width(10), .max('h3ff), .ongoal("wrap"), .trigger("rising"), .behavior("old")) counter_2 (
    .count(NEQ), .Q(counter_2_q), .clk(CLK), .clr(halt));  // open: load, D, carry, preset
  \七段显示译码器  \u_七段显示译码器_1  (
    .X3(Input[3]), .X2(Input[2]), .Seg_1(Out[0]), .X1(Input[1]), .X0(Input[0]), .Seg_2(Out[1]),
    .Seg_3(Out[2]), .Seg_4(Out[3]), .Seg_5(Out[4]), .Seg_6(Out[5]), .Seg_7(Out[6]));
  and and_1 (and_1_out, ~halt, NEQ);  // AND_Gate
  \七段显示译码器  \u_七段显示译码器_2  (
    .X3(input1[3]), .X2(input1[2]), .Seg_1(Out1[0]), .X1(input1[1]), .X0(input1[0]), .Seg_2(Out1[1]),
    .Seg_3(Out1[2]), .Seg_4(Out1[3]), .Seg_5(Out1[4]), .Seg_6(Out1[5]), .Seg_7(Out1[6]));
  RAM #(.addrWidth(10), .dataWidth(4), .bus("separate"), .Select("high")) ram_3 (
    .addr(counter_2_q), .din(Input), .str(and_1_out), .clk(CLK));  // open: data, sel, ld, clr
  _7_Segment_Display #(.active("true")) u_7_segment_display_1 (
    .g(multiplexer_1_out[15]), .f(multiplexer_1_out[14]), .a(multiplexer_1_out[13]),
    .b(multiplexer_1_out[12]), .e(multiplexer_1_out_2[15]), .d(multiplexer_1_out_2[14]),
    .c(multiplexer_1_out_2[13]), .dp(multiplexer_1_out_2[12]));
  Comparator #(.width(7), .mode("unsigned")) comparator_2 (.a(Out), .b(OutS), .eq(Equal));  // open: gt, lt
  _7_Segment_Display #(.active("true")) u_7_segment_display_2 (
    .g(multiplexer_1_out[11]), .f(multiplexer_1_out[10]), .a(multiplexer_1_out[9]), .b(multiplexer_1_out[8]),
    .e(multiplexer_1_out_2[11]), .d(multiplexer_1_out_2[10]), .c(multiplexer_1_out_2[9]),
    .dp(multiplexer_1_out_2[8]));
  _7_Segment_Display #(.active("true")) u_7_segment_display_3 (
    .g(multiplexer_1_out[7]), .f(multiplexer_1_out[6]), .a(multiplexer_1_out[5]), .b(multiplexer_1_out[4]),
    .e(multiplexer_1_out_2[7]), .d(multiplexer_1_out_2[6]), .c(multiplexer_1_out_2[5]),
    .dp(multiplexer_1_out_2[4]));
  D_Flip_Flop #(.trigger("rising"), .Pre_Clr_Positions("LEGACY"), .NegatePresetClear("false"), .enable("true"), .NewFFLayout("false")) d_ff_1 (
    .clk(CLK), .D(NEQ), .Q(d_ff_1_q), .Qn(d_ff_1_qn), .en(d_ff_1_qn));  // open: preset, reset
  Counter #(.width(16), .max('hffff), .ongoal("wrap"), .trigger("rising"), .behavior("old")) counter_3 (
    .count(nHalt), .Q(tunnel), .clk(CLK));  // open: load, D, carry, clr, preset
  Clock #(.highDuration(1), .lowDuration(1)) clock_1 (.out(CLK));
  Pull_Resistor #(.pull(0)) pull_resistor_1 (.node(Equal));
  not not_2 (NEQ, Equal);
  _7_Segment_Display #(.active("true")) u_7_segment_display_4 (
    .g(multiplexer_1_out[3]), .f(multiplexer_1_out[2]), .a(multiplexer_1_out[1]), .b(multiplexer_1_out[0]),
    .e(multiplexer_1_out_2[3]), .d(multiplexer_1_out_2[2]), .c(multiplexer_1_out_2[1]),
    .dp(multiplexer_1_out_2[0]));
  Multiplexer #(.select(1), .width(32), .disabled(0), .enable("true")) multiplexer_1 (
    .in0(32'h8a66ffee), .in1(32'h8a8cef44), .out({multiplexer_1_out_2, multiplexer_1_out}), .sel(d_ff_1_q),
    .en(halt));
  ROM #(.addrWidth(16), .dataWidth(4), .Select("high")) rom_1 (.addr(tunnel), .data(Input));
  ROM #(.addrWidth(16), .dataWidth(7), .Select("high")) rom_2 (.addr(tunnel), .data(OutS));

  // Notes on the sheet:
  //   测试节拍数
  //   测试标准输入输出数据获取
  //   错误记录X&Y
  //   存储器保存未通过的测试用例
  //   2位数无符号比较器自动测试
  //   标准输入输出数据
  //   ctrl+K驱动时钟自动测试
  //   contents of rom_1 (hex, n*v repeats v):
  //   0 1 2 3 4 5 6 7 8 9 a b c d e f
  //   contents of rom_2 (hex, n*v repeats v):
  //   7e 48 3d 6d 4b 67 77 4c 7f 6f 3f 6f 6f 67 77 6f
endmodule

module \_4位无符号比较器  (
  input  X3,
  input  X2,
  input  X1,
  input  X0,
  input  Y3,
  input  Y2,
  input  Y1,
  input  Y0,
  output Great,
  output Equal,
  output Less
);

  wire and_1_out, and_2_out, and_3_out, and_4_out, and_5_out, and_6_out, and_7_out, and_8_out, and_9_out,
       and_10_out, and_11_out, and_12_out, and_13_out, and_14_out, and_15_out, and_16_out, and_17_out,
       and_18_out, and_19_out, and_20_out, and_21_out, and_22_out, and_23_out, and_24_out, and_25_out,
       and_26_out, and_27_out, and_28_out, and_29_out, and_30_out, and_31_out, and_32_out, and_33_out,
       and_34_out, and_35_out, and_36_out, and_37_out, and_38_out, and_39_out, and_40_out, and_41_out,
       and_42_out, and_43_out, and_44_out, and_45_out, and_46_out, not_1_out, not_2_out, not_3_out,
       not_4_out, not_5_out, not_6_out, not_7_out, not_8_out, not_9_out, not_10_out, not_11_out, not_12_out,
       not_13_out, not_14_out, not_15_out, not_16_out, not_17_out, not_18_out, not_19_out, not_20_out,
       not_21_out, not_22_out, not_23_out, not_24_out, not_25_out, not_26_out, not_27_out, not_28_out,
       not_29_out, not_30_out, not_31_out, not_32_out, not_33_out, not_34_out, not_35_out, not_36_out,
       not_37_out, not_38_out, not_39_out, not_40_out, not_41_out, not_42_out, not_43_out, not_44_out,
       not_45_out, not_46_out, not_47_out, not_48_out, not_49_out, not_50_out, not_51_out, not_52_out,
       not_53_out, not_54_out, not_55_out, not_56_out, not_57_out, not_58_out, not_59_out, not_60_out,
       not_61_out, not_62_out, not_63_out, not_64_out, not_65_out, not_66_out, not_67_out, not_68_out,
       not_69_out, not_70_out, not_71_out, not_72_out, not_73_out, not_74_out, not_75_out, not_76_out,
       not_77_out, not_78_out, not_79_out, not_80_out, not_81_out, not_82_out, not_83_out, not_84_out,
       not_85_out, not_86_out, not_87_out, not_88_out, not_89_out, not_90_out, not_91_out, not_92_out,
       not_93_out, not_94_out, not_95_out, not_96_out, not_97_out, not_98_out, not_99_out, not_100_out,
       not_101_out, not_102_out, not_103_out, not_104_out, not_105_out, not_106_out, not_107_out,
       not_108_out, not_109_out, not_110_out, not_111_out, not_112_out, not_113_out, not_114_out,
       not_115_out, not_116_out, not_117_out, not_118_out, not_119_out, not_120_out, not_121_out,
       not_122_out, not_123_out, not_124_out, not_125_out, not_126_out, not_127_out, not_128_out;

  not not_1 (not_1_out, Y3);
  not not_2 (not_2_out, Y2);
  not not_3 (not_3_out, Y1);
  not not_4 (not_4_out, Y0);
  not not_5 (not_5_out, Y3);
  not not_6 (not_6_out, Y2);
  not not_7 (not_7_out, Y1);
  not not_8 (not_8_out, Y3);
  not not_9 (not_9_out, Y2);
  not not_10 (not_10_out, Y0);
  not not_11 (not_11_out, Y3);
  not not_12 (not_12_out, Y2);
  not not_13 (not_13_out, Y3);
  not not_14 (not_14_out, Y1);
  not not_15 (not_15_out, Y0);
  not not_16 (not_16_out, Y3);
  not not_17 (not_17_out, Y1);
  not not_18 (not_18_out, Y3);
  not not_19 (not_19_out, Y0);
  not not_20 (not_20_out, Y3);
  not not_21 (not_21_out, Y2);
  not not_22 (not_22_out, Y1);
  not not_23 (not_23_out, Y0);
  not not_24 (not_24_out, Y2);
  not not_25 (not_25_out, Y1);
  not not_26 (not_26_out, Y2);
  not not_27 (not_27_out, Y0);
  not not_28 (not_28_out, Y2);
  not not_29 (not_29_out, Y1);
  not not_30 (not_30_out, Y0);
  not not_31 (not_31_out, Y1);
  not not_32 (not_32_out, Y0);
  not not_33 (not_33_out, X3);
  not not_34 (not_34_out, X2);
  not not_35 (not_35_out, X1);
  not not_36 (not_36_out, X0);
  not not_37 (not_37_out, Y3);
  not not_38 (not_38_out, Y2);
  not not_39 (not_39_out, Y1);
  not not_40 (not_40_out, Y0);
  not not_41 (not_41_out, X3);
  not not_42 (not_42_out, X2);
  not not_43 (not_43_out, X1);
  not not_44 (not_44_out, Y3);
  not not_45 (not_45_out, Y2);
  not not_46 (not_46_out, Y1);
  not not_47 (not_47_out, X3);
  not not_48 (not_48_out, X2);
  not not_49 (not_49_out, X0);
  not not_50 (not_50_out, Y3);
  not not_51 (not_51_out, Y2);
  not not_52 (not_52_out, Y0);
  not not_53 (not_53_out, X3);
  not not_54 (not_54_out, X2);
  not not_55 (not_55_out, Y3);
  not not_56 (not_56_out, Y2);
  not not_57 (not_57_out, X3);
  not not_58 (not_58_out, X1);
  not not_59 (not_59_out, X0);
  not not_60 (not_60_out, Y3);
  not not_61 (not_61_out, Y1);
  not not_62 (not_62_out, Y0);
  not not_63 (not_63_out, X3);
  not not_64 (not_64_out, X1);
  not not_65 (not_65_out, Y3);
  not not_66 (not_66_out, Y1);
  not not_67 (not_67_out, X3);
  not not_68 (not_68_out, X0);
  not not_69 (not_69_out, Y3);
  not not_70 (not_70_out, Y0);
  not not_71 (not_71_out, X3);
  not not_72 (not_72_out, Y3);
  not not_73 (not_73_out, X2);
  not not_74 (not_74_out, X1);
  not not_75 (not_75_out, X0);
  not not_76 (not_76_out, Y2);
  not not_77 (not_77_out, Y1);
  not not_78 (not_78_out, Y0);
  not not_79 (not_79_out, X2);
  not not_80 (not_80_out, X1);
  not not_81 (not_81_out, Y2);
  not not_82 (not_82_out, Y1);
  not not_83 (not_83_out, X2);
  not not_84 (not_84_out, X0);
  not not_85 (not_85_out, Y2);
  not not_86 (not_86_out, Y0);
  not not_87 (not_87_out, X2);
  not not_88 (not_88_out, Y2);
  not not_89 (not_89_out, X1);
  not not_90 (not_90_out, X0);
  not not_91 (not_91_out, Y1);
  not not_92 (not_92_out, Y0);
  not not_93 (not_93_out, X1);
  not not_94 (not_94_out, Y1);
  not not_95 (not_95_out, X0);
  not not_96 (not_96_out, Y0);
  not not_97 (not_97_out, X3);
  not not_98 (not_98_out, X2);
  not not_99 (not_99_out, X1);
  not not_100 (not_100_out, X0);
  not not_101 (not_101_out, X3);
  not not_102 (not_102_out, X2);
  not not_103 (not_103_out, X1);
  not not_104 (not_104_out, X3);
  not not_105 (not_105_out, X2);
  not not_106 (not_106_out, X0);
  not not_107 (not_107_out, X3);
  not not_108 (not_108_out, X2);
  not not_109 (not_109_out, X3);
  not not_110 (not_110_out, X1);
  not not_111 (not_111_out, X0);
  not not_112 (not_112_out, X3);
  not not_113 (not_113_out, X1);
  not not_114 (not_114_out, X3);
  not not_115 (not_115_out, X0);
  not not_116 (not_116_out, X3);
  not not_117 (not_117_out, X2);
  not not_118 (not_118_out, X1);
  not not_119 (not_119_out, X0);
  not not_120 (not_120_out, X2);
  not not_121 (not_121_out, X1);
  not not_122 (not_122_out, X2);
  not not_123 (not_123_out, X0);
  not not_124 (not_124_out, X2);
  not not_125 (not_125_out, X1);
  not not_126 (not_126_out, X0);
  not not_127 (not_127_out, X1);
  not not_128 (not_128_out, X0);
  and and_1 (and_1_out, X0, not_1_out, not_2_out, not_3_out, not_4_out);
  and and_2 (and_2_out, X1, not_5_out, not_6_out, not_7_out);
  and and_3 (and_3_out, X1, X0, not_8_out, not_9_out, not_10_out);
  and and_4 (and_4_out, X2, not_11_out, not_12_out);
  and and_5 (and_5_out, X2, X0, not_13_out, not_14_out, not_15_out);
  and and_6 (and_6_out, X2, X1, not_16_out, not_17_out);
  and and_7 (and_7_out, X2, X1, X0, not_18_out, not_19_out);
  and and_8 (and_8_out, X3, not_20_out);
  and and_9 (and_9_out, X3, X0, not_21_out, not_22_out, not_23_out);
  and and_10 (and_10_out, X3, X1, not_24_out, not_25_out);
  and and_11 (and_11_out, X3, X1, X0, not_26_out, not_27_out);
  and and_12 (and_12_out, X3, X2, not_28_out);
  and and_13 (and_13_out, X3, X2, X0, not_29_out, not_30_out);
  and and_14 (and_14_out, X3, X2, X1, not_31_out);
  and and_15 (and_15_out, X3, X2, X1, X0, not_32_out);
  and and_16 (and_16_out, not_33_out, not_34_out, not_35_out, not_36_out, not_37_out, not_38_out, not_39_out, not_40_out);
  and and_17 (and_17_out, not_41_out, not_42_out, not_43_out, X0, not_44_out, not_45_out, not_46_out, Y0);
  and and_18 (and_18_out, not_47_out, not_48_out, X1, not_49_out, not_50_out, not_51_out, Y1, not_52_out);
  and and_19 (and_19_out, not_53_out, not_54_out, X1, X0, not_55_out, not_56_out, Y1, Y0);
  and and_20 (and_20_out, not_57_out, X2, not_58_out, not_59_out, not_60_out, Y2, not_61_out, not_62_out);
  and and_21 (and_21_out, not_63_out, X2, not_64_out, X0, not_65_out, Y2, not_66_out, Y0);
  and and_22 (and_22_out, not_67_out, X2, X1, not_68_out, not_69_out, Y2, Y1, not_70_out);
  and and_23 (and_23_out, not_71_out, X2, X1, X0, not_72_out, Y2, Y1, Y0);
  and and_24 (and_24_out, X3, not_73_out, not_74_out, not_75_out, Y3, not_76_out, not_77_out, not_78_out);
  and and_25 (and_25_out, X3, not_79_out, not_80_out, X0, Y3, not_81_out, not_82_out, Y0);
  and and_26 (and_26_out, X3, not_83_out, X1, not_84_out, Y3, not_85_out, Y1, not_86_out);
  and and_27 (and_27_out, X3, not_87_out, X1, X0, Y3, not_88_out, Y1, Y0);
  and and_28 (and_28_out, X3, X2, not_89_out, not_90_out, Y3, Y2, not_91_out, not_92_out);
  and and_29 (and_29_out, X3, X2, not_93_out, X0, Y3, Y2, not_94_out, Y0);
  and and_30 (and_30_out, X3, X2, X1, not_95_out, Y3, Y2, Y1, not_96_out);
  and and_31 (and_31_out, X3, X2, X1, X0, Y3, Y2, Y1, Y0);
  and and_32 (and_32_out, not_97_out, not_98_out, not_99_out, not_100_out, Y0);
  and and_33 (and_33_out, not_101_out, not_102_out, not_103_out, Y1);
  and and_34 (and_34_out, not_104_out, not_105_out, not_106_out, Y1, Y0);
  and and_35 (and_35_out, not_107_out, not_108_out, Y2);
  and and_36 (and_36_out, not_109_out, not_110_out, not_111_out, Y2, Y0);
  and and_37 (and_37_out, not_112_out, not_113_out, Y2, Y1);
  and and_38 (and_38_out, not_114_out, not_115_out, Y2, Y1, Y0);
  and and_39 (and_39_out, not_116_out, Y3);
  and and_40 (and_40_out, not_117_out, not_118_out, not_119_out, Y3, Y0);
  and and_41 (and_41_out, not_120_out, not_121_out, Y3, Y1);
  and and_42 (and_42_out, not_122_out, not_123_out, Y3, Y1, Y0);
  and and_43 (and_43_out, not_124_out, Y3, Y2);
  and and_44 (and_44_out, not_125_out, not_126_out, Y3, Y2, Y0);
  and and_45 (and_45_out, not_127_out, Y3, Y2, Y1);
  and and_46 (and_46_out, not_128_out, Y3, Y2, Y1, Y0);
  or or_1 (Great, and_1_out, and_2_out, and_3_out, and_4_out, and_5_out, and_6_out, and_7_out, and_8_out, and_9_out, and_10_out, and_11_out, and_12_out, and_13_out, and_14_out, and_15_out);
  or or_2 (Less, and_32_out, and_33_out, and_34_out, and_35_out, and_36_out, and_37_out, and_38_out, and_39_out, and_40_out, and_41_out, and_42_out, and_43_out, and_44_out, and_45_out, and_46_out);
  or or_3 (Equal, and_16_out, and_17_out, and_18_out, and_19_out, and_20_out, and_21_out, and_22_out, and_23_out, and_24_out, and_25_out, and_26_out, and_27_out, and_28_out, and_29_out, and_30_out, and_31_out);
endmodule

// 4位无符号比较器
module \_4位无符号比较器测试电路  (
  output [15:0] Cnt,
  output Y0,
  output X0,
  output Y1,
  output X1,
  output Y2,
  output X2,
  output Y3,
  output X3,
  output [2:0] Out,
  output _passed,
  output halt
);

  wire and_1_out, CLK, d_ff_1_q, d_ff_1_qn, NEQ, nHalt;
  wire [2:0] OutS;
  wire [9:0] counter_2_q;
  wire [15:0] multiplexer_1_out, multiplexer_1_out_2;

  Clock #(.highDuration(1), .lowDuration(1)) clock_1 (.out(CLK));
  Counter #(.width(16), .max('hffff), .ongoal("wrap"), .trigger("rising"), .behavior("old")) counter_1 (
    .count(nHalt), .Q(Cnt), .clk(CLK));  // open: load, D, carry, clr, preset
  // Probe on Cnt
  // Probe on Cnt
  // Probe on 16'hff
  Comparator #(.width(16), .mode("twosComplement")) comparator_1 (.a(Cnt), .b(16'hff), .eq(halt));  // open: gt, lt
  ROM #(.addrWidth(16), .dataWidth(8), .Select("high")) rom_1 (.addr(Cnt), .data({Y3, {3{Y0}}, X3, X2, X1, X0}));
  ROM #(.addrWidth(16), .dataWidth(3), .Select("high")) rom_2 (.addr(Cnt), .data(OutS));
  not not_1 (nHalt, halt);
  RAM #(.addrWidth(16), .dataWidth(3), .bus("separate"), .Select("low")) ram_1 (
    .addr(Cnt), .din(Out), .str(nHalt), .clk(CLK));  // open: data, sel, ld, clr
  \_4位无符号比较器  \u_4位无符号比较器_1  (
    .X3(X3), .X2(X2), .X1(X1), .X0(X0), .Y3(Y3), .Y2(Y0), .Y1(Y0), .Y0(Y0), .Great(Out[0]), .Equal(Out[1]),
    .Less(Out[2]));
  Comparator #(.width(3), .mode("twosComplement")) comparator_2 (.a(Out), .b(OutS), .eq(_passed));  // open: gt, lt
  Pull_Resistor #(.pull(0)) pull_resistor_1 (.node(_passed));
  not not_2 (NEQ, _passed);
  LED #(.active("true")) \u_测试完成  (.in(halt));
  Counter #(.width(10), .max('h3ff), .ongoal("wrap"), .trigger("rising"), .behavior("old")) counter_2 (
    .count(NEQ), .Q(counter_2_q), .clk(CLK), .clr(halt));  // open: load, D, carry, preset
  and and_1 (and_1_out, ~halt, NEQ);  // AND_Gate
  RAM #(.addrWidth(10), .dataWidth(8), .bus("separate"), .Select("high")) ram_2 (
    .addr(counter_2_q), .din({Y3, {3{Y0}}, X3, X2, X1, X0}), .str(and_1_out), .clk(CLK));  // open: data, sel, ld, clr
  _7_Segment_Display #(.active("true")) u_7_segment_display_1 (
    .g(multiplexer_1_out[11]), .f(multiplexer_1_out[10]), .a(multiplexer_1_out[9]), .b(multiplexer_1_out[8]),
    .e(multiplexer_1_out_2[11]), .d(multiplexer_1_out_2[10]), .c(multiplexer_1_out_2[9]),
    .dp(multiplexer_1_out_2[8]));
  _7_Segment_Display #(.active("true")) u_7_segment_display_2 (
    .g(multiplexer_1_out[15]), .f(multiplexer_1_out[14]), .a(multiplexer_1_out[13]),
    .b(multiplexer_1_out[12]), .e(multiplexer_1_out_2[15]), .d(multiplexer_1_out_2[14]),
    .c(multiplexer_1_out_2[13]), .dp(multiplexer_1_out_2[12]));
  D_Flip_Flop #(.trigger("rising"), .Pre_Clr_Positions("LEGACY"), .NegatePresetClear("false"), .enable("true"), .NewFFLayout("false")) d_ff_1 (
    .clk(CLK), .D(NEQ), .Q(d_ff_1_q), .Qn(d_ff_1_qn), .en(d_ff_1_qn));  // open: preset, reset
  _7_Segment_Display #(.active("true")) u_7_segment_display_3 (
    .g(multiplexer_1_out[3]), .f(multiplexer_1_out[2]), .a(multiplexer_1_out[1]), .b(multiplexer_1_out[0]),
    .e(multiplexer_1_out_2[3]), .d(multiplexer_1_out_2[2]), .c(multiplexer_1_out_2[1]),
    .dp(multiplexer_1_out_2[0]));
  _7_Segment_Display #(.active("true")) u_7_segment_display_4 (
    .g(multiplexer_1_out[7]), .f(multiplexer_1_out[6]), .a(multiplexer_1_out[5]), .b(multiplexer_1_out[4]),
    .e(multiplexer_1_out_2[7]), .d(multiplexer_1_out_2[6]), .c(multiplexer_1_out_2[5]),
    .dp(multiplexer_1_out_2[4]));
  Multiplexer #(.select(1), .width(32), .disabled(0), .enable("true")) multiplexer_1 (
    .in0(32'h8a66ffee), .in1(32'h8a8cef44), .out({multiplexer_1_out_2, multiplexer_1_out}), .sel(d_ff_1_q),
    .en(halt));

  assign Y1 = Y0;
  assign Y2 = Y0;

  // Other names for the same wires on the sheet: Equal = _passed; Input[7:0] = {Y3, {3{Y0}}, X3, X2, X1, X0};
  //   tunnel[15:0] = Cnt

  // Notes on the sheet:
  //   测试节拍数
  //   contents of rom_1 (hex, n*v repeats v):
  //   0 1 2 3 4 5 6 7 8 9 a b c d e f 10 11 12 13 14 15 16 17 18 19 1a 1b 1c 1d 1e 1f 20 21 22 23 24 25 26
  //   27 28 29 2a 2b 2c 2d 2e 2f 30 31 32 33 34 35 36 37 38 39 3a 3b 3c 3d 3e 3f 40 41 42 43 44 45 46 47
  //   48 49 4a 4b 4c 4d 4e 4f 50 51 52 53 54 55 56 57 58 59 5a 5b 5c 5d 5e 5f 60 61 62 63 64 65 66 67 68
  //   69 6a 6b 6c 6d 6e 6f 70 71 72 73 74 75 76 77 78 79 7a 7b 7c 7d 7e 7f 80 81 82 83 84 85 86 87 88 89
  //   8a 8b 8c 8d 8e 8f 90 91 92 93 94 95 96 97 98 99 9a 9b 9c 9d 9e 9f a0 a1 a2 a3 a4 a5 a6 a7 a8 a9 aa
  //   ab ac ad ae af b0 b1 b2 b3 b4 b5 b6 b7 b8 b9 ba bb bc bd be bf c0 c1 c2 c3 c4 c5 c6 c7 c8 c9 ca cb
  //   cc cd ce cf d0 d1 d2 d3 d4 d5 d6 d7 d8 d9 da db dc dd de df e0 e1 e2 e3 e4 e5 e6 e7 e8 e9 ea eb ec
  //   ed ee ef f0 f1 f2 f3 f4 f5 f6 f7 f8 f9 fa fb fc fd fe ff
  //   contents of rom_2 (hex, n*v repeats v):
  //   2 15*1 4 2 14*1 4 4 2 13*1 4 4 4 2 12*1 4*4 2 11*1 5*4 2 10*1 6*4 2 9*1 7*4 2 8*1 8*4 2 7*1 9*4 2
  //   6*1 10*4 2 5*1 11*4 2 4*1 12*4 2 1 1 1 13*4 2 1 1 14*4 2 1 15*4 2
  //   错误记录X&Y
  //   存储器保存未通过的测试用例
  //   4位数无符号比较器自动测试
  //   ctrl+K驱动时钟自动测试
endmodule

module \_8位无符号比较器  (
  input  [7:0] X,
  input  [7:0] Y,
  output Great,
  output Equal,
  output Less
);

  wire and_1_out, and_2_out, \n4位无符号比较器_1_equal , \n4位无符号比较器_1_great , \n4位无符号比较器_1_less ,
       \n4位无符号比较器_2_equal , \n4位无符号比较器_2_great , \n4位无符号比较器_2_less ;

  // Probe on X
  // Probe on Y
  \_4位无符号比较器  \u_4位无符号比较器_1  (
    .X3(X[7]), .X2(X[6]), .X1(X[5]), .X0(X[4]), .Y3(Y[7]), .Y2(Y[6]), .Y1(Y[5]), .Y0(Y[4]),
    .Great(\n4位无符号比较器_1_great ), .Equal(\n4位无符号比较器_1_equal ), .Less(\n4位无符号比较器_1_less ));
  \_4位无符号比较器  \u_4位无符号比较器_2  (
    .X3(X[3]), .X2(X[2]), .X1(X[1]), .X0(X[0]), .Y3(Y[3]), .Y2(Y[2]), .Y1(Y[1]), .Y0(Y[0]),
    .Great(\n4位无符号比较器_2_great ), .Equal(\n4位无符号比较器_2_equal ), .Less(\n4位无符号比较器_2_less ));
  and and_1 (and_1_out, \n4位无符号比较器_1_equal , \n4位无符号比较器_2_great );
  and and_2 (and_2_out, \n4位无符号比较器_1_equal , \n4位无符号比较器_2_less );
  or or_1 (Great, \n4位无符号比较器_1_great , and_1_out);
  and and_3 (Equal, \n4位无符号比较器_1_equal , \n4位无符号比较器_2_equal );
  or or_2 (Less, \n4位无符号比较器_1_less , and_2_out);

  // Other names for the same wires on the sheet: X0[3:0] = X[3:0]; X1[3:0] = X[7:4]; Y0[3:0] = Y[3:0];
  //   Y1[3:0] = Y[7:4]

  // Notes on the sheet:
  //   电路功能：X,Y进行无符号比较，Great=(X>Y)?1:0;
  //   输入引脚区
  //   输出引脚区
endmodule

module \_8位无符号比较器测试电路  (
  output [15:0] Cnt,
  output _passed,
  output halt
);

  wire and_1_out, CLK, d_ff_1_q, d_ff_1_qn, NEQ, nHalt;
  wire [2:0] Out, OutS;
  wire [9:0] counter_2_q;
  wire [15:0] Input, multiplexer_1_out, multiplexer_1_out_2;

  Clock #(.highDuration(1), .lowDuration(1)) clock_1 (.out(CLK));
  Counter #(.width(16), .max('hffff), .ongoal("wrap"), .trigger("rising"), .behavior("old")) counter_1 (
    .count(nHalt), .Q(Cnt), .clk(CLK));  // open: load, D, carry, clr, preset
  // Probe on Cnt
  // Probe on 16'hff
  // Probe on Cnt
  Comparator #(.width(16), .mode("twosComplement")) comparator_1 (.a(Cnt), .b(16'hff), .eq(halt));  // open: gt, lt
  ROM #(.addrWidth(16), .dataWidth(16), .Select("high")) rom_1 (.addr(Cnt), .data(Input));
  ROM #(.addrWidth(16), .dataWidth(3), .Select("high")) rom_2 (.addr(Cnt), .data(OutS));
  not not_1 (nHalt, halt);
  RAM #(.addrWidth(16), .dataWidth(3), .bus("separate"), .Select("low")) ram_1 (
    .addr(Cnt), .din(Out), .str(nHalt), .clk(CLK));  // open: data, sel, ld, clr
  \_8位无符号比较器  \u_8位无符号比较器_1  (.X(Input[7:0]), .Y(Input[15:8]), .Great(Out[0]), .Equal(Out[1]), .Less(Out[2]));
  Comparator #(.width(3), .mode("twosComplement")) comparator_2 (.a(Out), .b(OutS), .eq(_passed));  // open: gt, lt
  Pull_Resistor #(.pull(0)) pull_resistor_1 (.node(_passed));
  not not_2 (NEQ, _passed);
  LED #(.active("true")) \u_测试完成  (.in(halt));
  Counter #(.width(10), .max('h3ff), .ongoal("wrap"), .trigger("rising"), .behavior("old")) counter_2 (
    .count(NEQ), .Q(counter_2_q), .clk(CLK), .clr(halt));  // open: load, D, carry, preset
  and and_1 (and_1_out, ~halt, NEQ);  // AND_Gate
  RAM #(.addrWidth(10), .dataWidth(16), .bus("separate"), .Select("high")) ram_2 (
    .addr(counter_2_q), .din(Input), .str(and_1_out), .clk(CLK));  // open: data, sel, ld, clr
  _7_Segment_Display #(.active("true")) u_7_segment_display_1 (
    .g(multiplexer_1_out[11]), .f(multiplexer_1_out[10]), .a(multiplexer_1_out[9]), .b(multiplexer_1_out[8]),
    .e(multiplexer_1_out_2[11]), .d(multiplexer_1_out_2[10]), .c(multiplexer_1_out_2[9]),
    .dp(multiplexer_1_out_2[8]));
  _7_Segment_Display #(.active("true")) u_7_segment_display_2 (
    .g(multiplexer_1_out[15]), .f(multiplexer_1_out[14]), .a(multiplexer_1_out[13]),
    .b(multiplexer_1_out[12]), .e(multiplexer_1_out_2[15]), .d(multiplexer_1_out_2[14]),
    .c(multiplexer_1_out_2[13]), .dp(multiplexer_1_out_2[12]));
  D_Flip_Flop #(.trigger("rising"), .Pre_Clr_Positions("LEGACY"), .NegatePresetClear("false"), .enable("true"), .NewFFLayout("false")) d_ff_1 (
    .clk(CLK), .D(NEQ), .Q(d_ff_1_q), .Qn(d_ff_1_qn), .en(d_ff_1_qn));  // open: preset, reset
  _7_Segment_Display #(.active("true")) u_7_segment_display_3 (
    .g(multiplexer_1_out[7]), .f(multiplexer_1_out[6]), .a(multiplexer_1_out[5]), .b(multiplexer_1_out[4]),
    .e(multiplexer_1_out_2[7]), .d(multiplexer_1_out_2[6]), .c(multiplexer_1_out_2[5]),
    .dp(multiplexer_1_out_2[4]));
  _7_Segment_Display #(.active("true")) u_7_segment_display_4 (
    .g(multiplexer_1_out[3]), .f(multiplexer_1_out[2]), .a(multiplexer_1_out[1]), .b(multiplexer_1_out[0]),
    .e(multiplexer_1_out_2[3]), .d(multiplexer_1_out_2[2]), .c(multiplexer_1_out_2[1]),
    .dp(multiplexer_1_out_2[0]));
  Multiplexer #(.select(1), .width(32), .disabled(0), .enable("true")) multiplexer_1 (
    .in0(32'h8a66ffee), .in1(32'h8a8cef44), .out({multiplexer_1_out_2, multiplexer_1_out}), .sel(d_ff_1_q),
    .en(halt));

  // Other names for the same wires on the sheet: Equal = _passed; tunnel[15:0] = Cnt

  // Notes on the sheet:
  //   测试节拍数
  //   contents of rom_1 (hex, n*v repeats v):
  //   70 71 72 73 74 75 76 77 78 79 7a 7b 7c 7d 7e 7f 5550 5551 5552 5553 5554 5555 5556 5557 5558 5559
  //   555a 555b 555c 555d 555e 555f 3200 3201 3202 3203 3204 3205 3206 3207 3208 3209 320a 320b 320c 320d
  //   320e 320f 7e30 7e31 7e32 7e33 7e34 7e35 7e36 7e37 7e38 7e39 7e3a 7e3b 7e3c 7e3d 7e3e 7e3f ff30 ff31
  //   ff32 ff33 ff34 ff35 ff36 ff37 ff38 ff39 ff3a ff3b ff3c ff3d ff3e ff3f a630 a631 a632 a633 a634 a635
  //   a636 a637 a638 a639 a63a a63b a63c a63d a63e a63f cdd0 cdd1 cdd2 cdd3 cdd4 cdd5 cdd6 cdd7 cdd8 cdd9
  //   cdda cddb cddc cddd cdde cddf 1810 1811 1812 1813 1814 1815 1816 1817 1818 1819 181a 181b 181c 181d
  //   181e 181f 25a0 25a1 25a2 25a3 25a4 25a5 25a6 25a7 25a8 25a9 25aa 25ab 25ac 25ad 25ae 25af 4730 4731
  //   4732 4733 4734 4735 4736 4737 4738 4739 473a 473b 473c 473d 473e 473f 60c0 60c1 60c2 60c3 60c4 60c5
  //   60c6 60c7 60c8 60c9 60ca 60cb 60cc 60cd 60ce 60cf 9140 9141 9142 9143 9144 9145 9146 9147 9148 9149
  //   914a 914b 914c 914d 914e 914f 8d10 8d11 8d12 8d13 8d14 8d15 8d16 8d17 8d18 8d19 8d1a 8d1b 8d1c 8d1d
  //   8d1e 8d1f bf00 bf01 bf02 bf03 bf04 bf05 bf06 bf07 bf08 bf09 bf0a bf0b bf0c bf0d bf0e bf0f e2a0 e2a1
  //   e2a2 e2a3 e2a4 e2a5 e2a6 e2a7 e2a8 e2a9 e2aa e2ab e2ac e2ad e2ae e2af fee0 fee1 fee2 fee3 fee4 fee5
  //   fee6 fee7 fee8 fee9 feea feeb feec feed feee feef
  //   contents of rom_2 (hex, n*v repeats v):
  //   16*1 5*4 2 10*1 64*4 16*1 8*4 2 23*1 16*4 16*1 80*4
  //   错误记录X&Y
  //   存储器保存未通过的测试用例
  //   8位数无符号比较器自动测试
  //   ctrl+K驱动时钟自动测试
endmodule

module \_1位2路选择器  (
  input  X0,
  input  Sel,
  input  X1,
  output Out
);

  wire and_1_out, and_2_out, not_1_out;

  not not_1 (not_1_out, Sel);
  and and_1 (and_1_out, X0, not_1_out);
  and and_2 (and_2_out, X1, Sel);
  or or_1 (Out, and_1_out, and_2_out);

  // Notes on the sheet:
  //   输入引脚区
  //   电路功能：Out=(Sel==0)?X0:X1;
  //   请勿增删改引脚，请在下方利用上方输入输出引脚的隧道标签信号构建电路，ctrl+d复制选择组件
  //   输出引脚区
endmodule

module \_2路选择器_1位_测试电路  (
  output [15:0] Cnt,
  output X0,
  output X1,
  output Sel,
  output Out,
  output _passed,
  output halt
);

  wire and_1_out, CLK, d_ff_1_q, d_ff_1_qn, NEQ, nHalt, OutS;
  wire [9:0] counter_2_q;
  wire [15:0] multiplexer_1_out, multiplexer_1_out_2;

  Clock #(.highDuration(1), .lowDuration(1)) clock_1 (.out(CLK));
  Counter #(.width(16), .max('hffff), .ongoal("wrap"), .trigger("rising"), .behavior("old")) counter_1 (
    .count(nHalt), .Q(Cnt), .clk(CLK));  // open: load, D, carry, clr, preset
  // Probe on Cnt
  // Probe on Cnt
  // Probe on 16'h8
  Comparator #(.width(16), .mode("twosComplement")) comparator_1 (.a(Cnt), .b(16'h8), .eq(halt));  // open: gt, lt
  ROM #(.addrWidth(16), .dataWidth(3), .Select("high")) rom_1 (.addr(Cnt), .data({Sel, X1, X0}));
  ROM #(.addrWidth(16), .dataWidth(1), .Select("high")) rom_2 (.addr(Cnt), .data(OutS));
  not not_1 (nHalt, halt);
  RAM #(.addrWidth(16), .dataWidth(1), .bus("separate"), .Select("low")) ram_1 (
    .addr(Cnt), .din(Out), .str(nHalt), .clk(CLK));  // open: data, sel, ld, clr
  \_1位2路选择器  \u_1位2路选择器_1  (.X0(X0), .X1(X1), .Sel(Sel), .Out(Out));
  Comparator #(.width(1), .mode("twosComplement")) comparator_2 (.a(Out), .b(OutS), .eq(_passed));  // open: gt, lt
  Pull_Resistor #(.pull(0)) pull_resistor_1 (.node(_passed));
  not not_2 (NEQ, _passed);
  LED #(.active("true")) \u_测试完成  (.in(halt));
  Counter #(.width(10), .max('h3ff), .ongoal("wrap"), .trigger("rising"), .behavior("old")) counter_2 (
    .count(NEQ), .Q(counter_2_q), .clk(CLK), .clr(halt));  // open: load, D, carry, preset
  and and_1 (and_1_out, ~halt, NEQ);  // AND_Gate
  RAM #(.addrWidth(10), .dataWidth(3), .bus("separate"), .Select("high")) ram_2 (
    .addr(counter_2_q), .din({Sel, X1, X0}), .str(and_1_out), .clk(CLK));  // open: data, sel, ld, clr
  _7_Segment_Display #(.active("true")) u_7_segment_display_1 (
    .g(multiplexer_1_out[11]), .f(multiplexer_1_out[10]), .a(multiplexer_1_out[9]), .b(multiplexer_1_out[8]),
    .e(multiplexer_1_out_2[11]), .d(multiplexer_1_out_2[10]), .c(multiplexer_1_out_2[9]),
    .dp(multiplexer_1_out_2[8]));
  _7_Segment_Display #(.active("true")) u_7_segment_display_2 (
    .g(multiplexer_1_out[15]), .f(multiplexer_1_out[14]), .a(multiplexer_1_out[13]),
    .b(multiplexer_1_out[12]), .e(multiplexer_1_out_2[15]), .d(multiplexer_1_out_2[14]),
    .c(multiplexer_1_out_2[13]), .dp(multiplexer_1_out_2[12]));
  D_Flip_Flop #(.trigger("rising"), .Pre_Clr_Positions("LEGACY"), .NegatePresetClear("false"), .enable("true"), .NewFFLayout("false")) d_ff_1 (
    .clk(CLK), .D(NEQ), .Q(d_ff_1_q), .Qn(d_ff_1_qn), .en(d_ff_1_qn));  // open: preset, reset
  _7_Segment_Display #(.active("true")) u_7_segment_display_3 (
    .g(multiplexer_1_out[7]), .f(multiplexer_1_out[6]), .a(multiplexer_1_out[5]), .b(multiplexer_1_out[4]),
    .e(multiplexer_1_out_2[7]), .d(multiplexer_1_out_2[6]), .c(multiplexer_1_out_2[5]),
    .dp(multiplexer_1_out_2[4]));
  _7_Segment_Display #(.active("true")) u_7_segment_display_4 (
    .g(multiplexer_1_out[3]), .f(multiplexer_1_out[2]), .a(multiplexer_1_out[1]), .b(multiplexer_1_out[0]),
    .e(multiplexer_1_out_2[3]), .d(multiplexer_1_out_2[2]), .c(multiplexer_1_out_2[1]),
    .dp(multiplexer_1_out_2[0]));
  Multiplexer #(.select(1), .width(32), .disabled(0), .enable("true")) multiplexer_1 (
    .in0(32'h8a66ffee), .in1(32'h8a8cef44), .out({multiplexer_1_out_2, multiplexer_1_out}), .sel(d_ff_1_q),
    .en(halt));

  // Other names for the same wires on the sheet: Equal = _passed; Input[2:0] = {Sel, X1, X0}; tunnel[15:0] = Cnt

  // Notes on the sheet:
  //   测试节拍数
  //   contents of rom_1 (hex, n*v repeats v):
  //   0 1 2 3 4 5 6 7 0 1
  //   contents of rom_2 (hex, n*v repeats v):
  //   0 1 0 1 0 0 1 1
  //   错误记录X&Y
  //   存储器保存未通过的测试用例
  //   2路选择器（1位）自动测试
  //   ctrl+K驱动时钟自动测试
endmodule

module \_8位2路选择器  (
  input  [7:0] X,
  input  Sel,
  input  [7:0] Y,
  output [7:0] Out
);

  wire [7:0] and_1_out, and_2_out, not_1_out;

  // Probe on X
  // Probe on Y
  assign not_1_out = ~{8{Sel}};  // NOT_Gate not_1, 8 bits wide
  assign and_1_out = X & not_1_out;  // AND_Gate and_1, 8 bits wide
  assign and_2_out = Y & {8{Sel}};  // AND_Gate and_2, 8 bits wide
  assign Out = and_1_out | and_2_out;  // OR_Gate or_1, 8 bits wide
  // Probe on Out

  // Notes on the sheet:
  //   输入引脚区
  //   电路功能：Out=(Sel==0)?X:Y;
  //   请勿增删改引脚，请在下方利用上方输入输出引脚的隧道标签信号构建电路，ctrl+d复制选择组件
  //   输出引脚区
endmodule

module \_8位2路选择器测试电路  (
  output [7:0] Cnt,
  output [7:0] X0,
  output [7:0] X1,
  output Sel,
  output [7:0] Out,
  output _passed,
  output halt
);

  wire and_1_out, CLK, d_ff_1_q, d_ff_1_qn, NEQ, nHalt;
  wire [2:0] Input;
  wire [7:0] OutS;
  wire [9:0] counter_2_q;
  wire [15:0] multiplexer_1_out, multiplexer_1_out_2;

  Clock #(.highDuration(1), .lowDuration(1)) clock_1 (.out(CLK));
  Counter #(.width(8), .max('hff), .ongoal("wrap"), .trigger("rising"), .behavior("old")) counter_1 (
    .count(nHalt), .Q(Cnt), .clk(CLK));  // open: load, D, carry, clr, preset
  // Probe on Cnt
  // Probe on Cnt
  // Probe on 8'hfe
  Comparator #(.width(8), .mode("twosComplement")) comparator_1 (.a(Cnt), .b(8'hfe), .eq(halt));  // open: gt, lt
  ROM #(.addrWidth(8), .dataWidth(8), .Select("high")) rom_1 (.addr(Cnt), .data(X0));
  ROM #(.addrWidth(8), .dataWidth(8), .Select("high")) rom_2 (.addr(Cnt), .data(X1));
  ROM #(.addrWidth(8), .dataWidth(1), .Select("high")) rom_3 (.addr(Cnt), .data(Sel));
  ROM #(.addrWidth(8), .dataWidth(8), .Select("high")) rom_4 (.addr(Cnt), .data(OutS));
  not not_1 (nHalt, halt);
  RAM #(.addrWidth(8), .dataWidth(8), .bus("separate"), .Select("low")) ram_1 (
    .addr(Cnt), .din(Out), .str(nHalt), .clk(CLK));  // open: data, sel, ld, clr
  Comparator #(.width(8), .mode("twosComplement")) comparator_2 (.a(Out), .b(OutS), .eq(_passed));  // open: gt, lt
  \_8位2路选择器  \u_8位2路选择器_1  (.X(X0), .Sel(Sel), .Y(X1), .Out(Out));
  Pull_Resistor #(.pull(0)) pull_resistor_1 (.node(_passed));
  not not_2 (NEQ, _passed);
  LED #(.active("true")) \u_测试完成  (.in(halt));
  Counter #(.width(10), .max('h3ff), .ongoal("wrap"), .trigger("rising"), .behavior("old")) counter_2 (
    .count(NEQ), .Q(counter_2_q), .clk(CLK), .clr(halt));  // open: load, D, carry, preset
  and and_1 (and_1_out, ~halt, NEQ);  // AND_Gate
  RAM #(.addrWidth(10), .dataWidth(3), .bus("separate"), .Select("high")) ram_2 (
    .addr(counter_2_q), .din(Input), .str(and_1_out), .clk(CLK));  // open: data, sel, ld, clr
  _7_Segment_Display #(.active("true")) u_7_segment_display_1 (
    .g(multiplexer_1_out[11]), .f(multiplexer_1_out[10]), .a(multiplexer_1_out[9]), .b(multiplexer_1_out[8]),
    .e(multiplexer_1_out_2[11]), .d(multiplexer_1_out_2[10]), .c(multiplexer_1_out_2[9]),
    .dp(multiplexer_1_out_2[8]));
  _7_Segment_Display #(.active("true")) u_7_segment_display_2 (
    .g(multiplexer_1_out[15]), .f(multiplexer_1_out[14]), .a(multiplexer_1_out[13]),
    .b(multiplexer_1_out[12]), .e(multiplexer_1_out_2[15]), .d(multiplexer_1_out_2[14]),
    .c(multiplexer_1_out_2[13]), .dp(multiplexer_1_out_2[12]));
  D_Flip_Flop #(.trigger("rising"), .Pre_Clr_Positions("LEGACY"), .NegatePresetClear("false"), .enable("true"), .NewFFLayout("false")) d_ff_1 (
    .clk(CLK), .D(NEQ), .Q(d_ff_1_q), .Qn(d_ff_1_qn), .en(d_ff_1_qn));  // open: preset, reset
  _7_Segment_Display #(.active("true")) u_7_segment_display_3 (
    .g(multiplexer_1_out[7]), .f(multiplexer_1_out[6]), .a(multiplexer_1_out[5]), .b(multiplexer_1_out[4]),
    .e(multiplexer_1_out_2[7]), .d(multiplexer_1_out_2[6]), .c(multiplexer_1_out_2[5]),
    .dp(multiplexer_1_out_2[4]));
  _7_Segment_Display #(.active("true")) u_7_segment_display_4 (
    .g(multiplexer_1_out[3]), .f(multiplexer_1_out[2]), .a(multiplexer_1_out[1]), .b(multiplexer_1_out[0]),
    .e(multiplexer_1_out_2[3]), .d(multiplexer_1_out_2[2]), .c(multiplexer_1_out_2[1]),
    .dp(multiplexer_1_out_2[0]));
  Multiplexer #(.select(1), .width(32), .disabled(0), .enable("true")) multiplexer_1 (
    .in0(32'h8a66ffee), .in1(32'h8a8cef44), .out({multiplexer_1_out_2, multiplexer_1_out}), .sel(d_ff_1_q),
    .en(halt));

  // Other names for the same wires on the sheet: Equal = _passed; tunnel[7:0] = Cnt

  // Notes on the sheet:
  //   测试节拍数
  //   contents of rom_1 (hex, n*v repeats v):
  //   6 d6 e2 ef f0 76 21 fb ca b2 68 6f 7b 7c ee bb 95 98 31 49 90 e1 31 b3 4 83 b1 8 f1 3f 7b c f9 ac 99
  //   76 a2 71 9d 32 95 8d db 9d e3 91 ab cd 3b e1 a9 c7 36 f7 f6 c8 8d a1 76 7e 5e 3f 10 4c 6c 7 f2 8b 5c
  //   42 cb c5 fa 8d 10 f9 74 1a 39 db 9a ee 2 12 25 22 ac 79 ee 23 3b 60 33 f3 b6 c9 d7 67 6b ac a0 68 2a
  //   35 78 33 86 2 ae 99 18 67 33 41 bc aa dd e2 d3 48 a9 8b 81 2f f2 dd ee 3 bc 4c 86 5b ed 62 39 2 8f
  //   fd bc 38 11 8d c8 ef 84 58 57 f df b7 eb b4 3c 58 c8 6b 19 7b 36 7a 9a 36 c1 17 c3 b2 7a ac bf 6c 34
  //   1a 1d 76 c8 f4 e b5 53 c1 a9 21 74 3c 28 a 90 95 2a 4e f ae f0 a5 9d 5f a2 d6 6b b3 88 0 6d 2a 52 d4
  //   9a f7 51 d6 30 40 bc a1 ee 62 ee 20 59 2b a3 d7 fa 1f 40 19 9b b5 9 50 8e 98 6a 3a e6 e7 30 27 bd 76
  //   cd 3d 6e c 99 b5 d9 a5 c 1c a4 ae 6 94 75
  //   contents of rom_2 (hex, n*v repeats v):
  //   7 a4 e2 9b b6 12 bb 1f 24 38 c1 fb 8 6 e3 67 d5 e e9 df f4 c6 aa 63 ff c7 55 b9 5 11 ab a7 ca 46 40
  //   3b 5 ec bf 4 a2 ac 24 57 fe 96 0 8c 2f 5c b9 3f 3a 94 c9 90 5c f8 fb 65 43 a6 b2 a4 52 61 23 7b e2
  //   ce 98 99 7d b9 ac 73 22 4f 92 81 85 63 4f 80 4d ab fc ae 55 1 6 12 ed a3 6f b3 17 74 b dc cc 3a c5
  //   60 35 df d9 d1 f3 b1 19 c8 59 a3 29 22 ad 8b c4 3e 6c 63 f6 40 84 8a 60 52 99 1 78 df 42 af c8 d7 4a
  //   9e 2b f0 f1 3c 15 e0 29 9d c9 a5 da b5 a1 be 20 9f 4a 6f 88 d9 6 2 58 86 ea 2 c6 ad 1f 80 3c 76 23
  //   4f 9c 70 6 49 76 cf ad 88 54 a7 13 af f0 33 84 20 7a 12 e2 44 d4 85 e1 c7 d6 b3 4c da 8b e7 3f 70 73
  //   cd 6b 83 c1 ba 57 4d 9b e2 9a 91 5e a0 23 d1 d8 b3 72 96 8d 7d dd ac f4 43 ce 64 b8 71 0 d2 f8 d3 c6
  //   d 88 de 45 73 2f e6 b6 e4 e9 67 a7 3 23 3e 38
  //   contents of rom_3 (hex, n*v repeats v):
  //   1 0 7*1 0 0 1 1 0 1 0 6*1 0 1 0 0 1 0 1 0 0 1 0 1 1 1 0 1 1 1 0 1 1 0 1 8*0 1 1 4*0 1 1 1 0 0 0 1 1
  //   0 1 0 0 1 1 1 0 4*1 0 1 0 1 1 0 1 0 0 0 1 0 1 1 0 1 0 1 0 1 4*0 1 1 0 4*1 4*0 1 0 1 1 1 0 1 0 1 0 1
  //   1 0 1 1 0 1 0 1 1 1 0 0 0 1 1 0 1 6*0 1 1 0 0 0 1 1 0 0 6*1 0 0 1 1 0 0 1 1 1 0 1 1 0 0 1 0 0 0 4*1
  //   0 1 1 0 1 1 0 1 0 1 1 1 0 0 0 1 0 1 1 6*0 1 0 0 1 0 1 0 5*1 0 0 0 1 0 1 4*0 1 1 0 1 0 0 1 0 1 1 1 0
  //   5*1 0 0 1
  //   contents of rom_4 (hex, n*v repeats v):
  //   7 d6 e2 9b b6 12 bb 1f 24 b2 68 fb 8 7c e3 bb d5 e e9 df f4 c6 31 63 4 83 55 8 5 3f 7b a7 f9 46 40
  //   3b a2 ec bf 4 95 ac 24 9d fe 91 ab cd 3b e1 a9 c7 36 94 c9 c8 8d a1 76 65 43 a6 10 4c 6c 61 23 8b e2
  //   42 cb 99 7d b9 10 73 22 4f 92 db 85 ee 4f 80 25 ab ac 79 ee 1 3b 12 ed f3 6f c9 17 67 b ac a0 68 2a
  //   60 35 33 d9 d1 f3 b1 18 67 33 41 29 aa ad 8b c4 48 6c 8b f6 2f 84 8a ee 52 99 4c 78 5b 42 af c8 2 8f
  //   fd 2b f0 11 3c c8 ef 84 58 57 f da b5 eb b4 3c 9f 4a 6b 19 d9 6 2 58 86 ea 17 c3 ad 1f ac bf 76 23
  //   4f 1d 70 6 f4 e cf 53 c1 a9 a7 13 af f0 a 84 20 2a 12 e2 ae d4 a5 e1 c7 d6 d6 6b b3 8b 0 3f 70 52 d4
  //   9a f7 51 d6 57 40 bc e2 ee 91 ee a0 23 d1 d8 b3 fa 1f 40 7d 9b ac 9 50 8e 98 b8 71 e6 d2 30 27 c6 76
  //   88 de 45 c 2f e6 b6 e4 e9 1c a4 3 6 94 75
  //   错误记录X&Y
  //   存储器保存未通过的测试用例
  //   2路选择器（8位）自动测试
  //   ctrl+K驱动时钟自动测试
endmodule

module \模十可逆计数器激励函数  (
  input  y3,
  input  y2,
  input  y1,
  input  y0,
  input  Mode,
  output D3,
  output D2,
  output D1,
  output D0
);

  wire and_1_out, and_2_out, and_3_out, and_4_out, and_5_out, and_6_out, and_7_out, and_8_out, and_9_out,
       and_10_out, and_11_out, and_12_out, and_13_out, and_14_out, and_15_out, and_16_out, not_1_out,
       not_2_out, not_3_out, not_4_out, not_5_out, not_6_out, not_7_out, not_8_out, not_9_out, not_10_out,
       not_11_out, not_12_out, not_13_out, not_14_out, not_15_out, not_16_out, not_17_out, not_18_out,
       not_19_out, not_20_out, not_21_out, not_22_out, not_23_out, not_24_out, not_25_out, not_26_out,
       not_27_out, not_28_out, not_29_out, not_30_out, not_31_out, not_32_out, not_33_out, not_34_out,
       not_35_out, not_36_out, not_37_out, not_38_out, not_39_out, not_40_out, not_41_out, not_42_out;

  not not_1 (not_1_out, y3);
  not not_2 (not_2_out, y2);
  not not_3 (not_3_out, y1);
  not not_4 (not_4_out, y0);
  not not_5 (not_5_out, y3);
  not not_6 (not_6_out, Mode);
  not not_7 (not_7_out, y2);
  not not_8 (not_8_out, y1);
  not not_9 (not_9_out, y0);
  not not_10 (not_10_out, Mode);
  not not_11 (not_11_out, y2);
  not not_12 (not_12_out, y1);
  not not_13 (not_13_out, y3);
  not not_14 (not_14_out, y2);
  not not_15 (not_15_out, Mode);
  not not_16 (not_16_out, y3);
  not not_17 (not_17_out, y1);
  not not_18 (not_18_out, Mode);
  not not_19 (not_19_out, y3);
  not not_20 (not_20_out, y3);
  not not_21 (not_21_out, y0);
  not not_22 (not_22_out, y2);
  not not_23 (not_23_out, y1);
  not not_24 (not_24_out, y0);
  not not_25 (not_25_out, y3);
  not not_26 (not_26_out, y1);
  not not_27 (not_27_out, Mode);
  not not_28 (not_28_out, y3);
  not not_29 (not_29_out, y0);
  not not_30 (not_30_out, Mode);
  not not_31 (not_31_out, y3);
  not not_32 (not_32_out, y3);
  not not_33 (not_33_out, y1);
  not not_34 (not_34_out, y0);
  not not_35 (not_35_out, y2);
  not not_36 (not_36_out, y1);
  not not_37 (not_37_out, y0);
  not not_38 (not_38_out, y3);
  not not_39 (not_39_out, y0);
  not not_40 (not_40_out, y2);
  not not_41 (not_41_out, y1);
  not not_42 (not_42_out, y0);
  and and_1 (and_1_out, not_1_out, not_2_out, not_3_out, not_4_out, Mode);
  and and_2 (and_2_out, not_5_out, y2, y1, y0, not_6_out);
  and and_3 (and_3_out, y3, not_7_out, not_8_out, not_9_out, not_10_out);
  and and_4 (and_4_out, y3, not_11_out, not_12_out, y0, Mode);
  and and_5 (and_5_out, not_13_out, not_14_out, y1, y0, not_15_out);
  and and_6 (and_6_out, not_16_out, y2, not_17_out, not_18_out);
  and and_7 (and_7_out, not_19_out, y2, y0, Mode);
  and and_8 (and_8_out, not_20_out, y2, y1, not_21_out);
  and and_9 (and_9_out, y3, not_22_out, not_23_out, not_24_out, Mode);
  and and_10 (and_10_out, not_25_out, not_26_out, y0, not_27_out);
  and and_11 (and_11_out, not_28_out, y1, not_29_out, not_30_out);
  and and_12 (and_12_out, not_31_out, y1, y0, Mode);
  and and_13 (and_13_out, not_32_out, y2, not_33_out, not_34_out, Mode);
  and and_14 (and_14_out, y3, not_35_out, not_36_out, not_37_out, Mode);
  and and_15 (and_15_out, not_38_out, not_39_out);
  and and_16 (and_16_out, not_40_out, not_41_out, not_42_out);
  or or_1 (D3, and_1_out, and_2_out, and_3_out, and_4_out);
  or or_2 (D2, and_5_out, and_6_out, and_7_out, and_8_out, and_9_out);
  or or_3 (D1, and_10_out, and_11_out, and_12_out, and_13_out, and_14_out);
  or or_4 (D0, and_15_out, and_16_out);
endmodule

module \模十可逆计数器激励函数测试电路  (
  output [7:0] Cnt,
  output [3:0] S,
  output Mode,
  output [3:0] NS,
  output _passed,
  output halt
);

  wire and_1_out, CLK, d_ff_1_q, d_ff_1_qn, NEQ, nHalt;
  wire [3:0] NSs;
  wire [9:0] counter_2_q;
  wire [15:0] multiplexer_1_out, multiplexer_1_out_2;

  Clock #(.highDuration(1), .lowDuration(1)) clock_1 (.out(CLK));
  Counter #(.width(8), .max('hff), .ongoal("wrap"), .trigger("rising"), .behavior("old")) counter_1 (
    .count(nHalt), .Q(Cnt), .clk(CLK));  // open: load, D, carry, clr, preset
  // Probe on Cnt
  // Probe on Cnt
  // Probe on 8'h13
  Comparator #(.width(8), .mode("twosComplement")) comparator_1 (.a(Cnt), .b(8'h13), .eq(halt));  // open: gt, lt
  ROM #(.addrWidth(8), .dataWidth(4), .Select("high")) rom_1 (.addr(Cnt), .data(S));
  ROM #(.addrWidth(8), .dataWidth(1), .Select("high")) rom_2 (.addr(Cnt), .data(Mode));
  ROM #(.addrWidth(8), .dataWidth(4), .Select("high")) rom_3 (.addr(Cnt), .data(NSs));
  not not_1 (nHalt, halt);
  RAM #(.addrWidth(8), .dataWidth(4), .bus("separate"), .Select("low")) ram_1 (
    .addr(Cnt), .din(NS), .str(nHalt), .clk(CLK));  // open: data, sel, ld, clr
  Comparator #(.width(4), .mode("twosComplement")) comparator_2 (.a(NS), .b(NSs), .eq(_passed));  // open: gt, lt
  LED #(.active("true")) \u_测试完成  (.in(halt));
  Counter #(.width(10), .max('h3ff), .ongoal("wrap"), .trigger("rising"), .behavior("old")) counter_2 (
    .count(NEQ), .Q(counter_2_q), .clk(CLK), .clr(halt));  // open: load, D, carry, preset
  \模十可逆计数器激励函数  \u_模十可逆计数器激励函数_1  (
    .y3(S[3]), .y2(S[2]), .y1(S[1]), .y0(S[0]), .D3(NS[3]), .Mode(Mode), .D2(NS[2]), .D1(NS[1]), .D0(NS[0]));
  Pull_Resistor #(.pull(0)) pull_resistor_1 (.node(_passed));
  not not_2 (NEQ, _passed);
  and and_1 (and_1_out, ~halt, NEQ);  // AND_Gate
  RAM #(.addrWidth(10), .dataWidth(4), .bus("separate"), .Select("high")) ram_2 (
    .addr(counter_2_q), .din(NS), .str(and_1_out), .clk(CLK));  // open: data, sel, ld, clr
  _7_Segment_Display #(.active("true")) u_7_segment_display_1 (
    .g(multiplexer_1_out[15]), .f(multiplexer_1_out[14]), .a(multiplexer_1_out[13]),
    .b(multiplexer_1_out[12]), .e(multiplexer_1_out_2[15]), .d(multiplexer_1_out_2[14]),
    .c(multiplexer_1_out_2[13]), .dp(multiplexer_1_out_2[12]));
  _7_Segment_Display #(.active("true")) u_7_segment_display_2 (
    .g(multiplexer_1_out[11]), .f(multiplexer_1_out[10]), .a(multiplexer_1_out[9]), .b(multiplexer_1_out[8]),
    .e(multiplexer_1_out_2[11]), .d(multiplexer_1_out_2[10]), .c(multiplexer_1_out_2[9]),
    .dp(multiplexer_1_out_2[8]));
  D_Flip_Flop #(.trigger("rising"), .Pre_Clr_Positions("LEGACY"), .NegatePresetClear("false"), .enable("true"), .NewFFLayout("false")) d_ff_1 (
    .clk(CLK), .D(NEQ), .Q(d_ff_1_q), .Qn(d_ff_1_qn), .en(d_ff_1_qn));  // open: preset, reset
  _7_Segment_Display #(.active("true")) u_7_segment_display_3 (
    .g(multiplexer_1_out[7]), .f(multiplexer_1_out[6]), .a(multiplexer_1_out[5]), .b(multiplexer_1_out[4]),
    .e(multiplexer_1_out_2[7]), .d(multiplexer_1_out_2[6]), .c(multiplexer_1_out_2[5]),
    .dp(multiplexer_1_out_2[4]));
  _7_Segment_Display #(.active("true")) u_7_segment_display_4 (
    .g(multiplexer_1_out[3]), .f(multiplexer_1_out[2]), .a(multiplexer_1_out[1]), .b(multiplexer_1_out[0]),
    .e(multiplexer_1_out_2[3]), .d(multiplexer_1_out_2[2]), .c(multiplexer_1_out_2[1]),
    .dp(multiplexer_1_out_2[0]));
  Multiplexer #(.select(1), .width(32), .disabled(0), .enable("true")) multiplexer_1 (
    .in0(32'h8a66ffee), .in1(32'h8a8cef44), .out({multiplexer_1_out_2, multiplexer_1_out}), .sel(d_ff_1_q),
    .en(halt));

  // Other names for the same wires on the sheet: Equal = _passed; tunnel[7:0] = Cnt

  // Notes on the sheet:
  //   测试节拍数
  //   contents of rom_1 (hex, n*v repeats v):
  //   0 1 2 3 4 5 6 7 8 9 9 8 7 6 5 4 3 2 1
  //   contents of rom_2 (hex, n*v repeats v):
  //   10*0 17*1
  //   contents of rom_3 (hex, n*v repeats v):
  //   1 2 3 4 5 6 7 8 9 0 8 7 6 5 4 3 2 1 0 8*9 227*1
  //   错误记录X&Y
  //   存储器保存未通过的测试用例
  //   模十可逆计数器状态转换自动测试
  //   ctrl+K驱动时钟自动测试
endmodule

module \模十可逆计数器输出函数  (
  input  S3,
  input  S2,
  input  S1,
  input  S0,
  input  Mode,
  output Cout
);

  wire and_1_out, and_2_out, not_1_out, not_2_out, not_3_out, not_4_out, not_5_out, not_6_out, not_7_out;

  not not_1 (not_1_out, S3);
  not not_2 (not_2_out, S2);
  not not_3 (not_3_out, S1);
  not not_4 (not_4_out, S0);
  not not_5 (not_5_out, S2);
  not not_6 (not_6_out, S1);
  not not_7 (not_7_out, Mode);
  and and_1 (and_1_out, not_1_out, not_2_out, not_3_out, not_4_out, Mode);
  and and_2 (and_2_out, S3, not_5_out, not_6_out, S0, not_7_out);
  or or_1 (Cout, and_1_out, and_2_out);
endmodule

module \模十可逆计数器输出函数测试电路  (
  output [7:0] Cnt,
  output [3:0] S,
  output Mode,
  output Cout,
  output _passed,
  output halt
);

  wire and_1_out, CLK, CoutS, d_ff_1_q, d_ff_1_qn, NEQ, nHalt;
  wire [9:0] counter_2_q;
  wire [15:0] multiplexer_1_out, multiplexer_1_out_2;

  Clock #(.highDuration(1), .lowDuration(1)) clock_1 (.out(CLK));
  Counter #(.width(8), .max('hff), .ongoal("wrap"), .trigger("rising"), .behavior("old")) counter_1 (
    .count(nHalt), .Q(Cnt), .clk(CLK));  // open: load, D, carry, clr, preset
  // Probe on Cnt
  // Probe on Cnt
  // Probe on 8'h20
  Comparator #(.width(8), .mode("twosComplement")) comparator_1 (.a(Cnt), .b(8'h20), .eq(halt));  // open: gt, lt
  ROM #(.addrWidth(8), .dataWidth(5), .Select("high")) rom_1 (.addr(Cnt), .data({Mode, S}));
  ROM #(.addrWidth(8), .dataWidth(1), .Select("high")) rom_2 (.addr(Cnt), .data(CoutS));
  not not_1 (nHalt, halt);
  RAM #(.addrWidth(8), .dataWidth(1), .bus("separate"), .Select("low")) ram_1 (
    .addr(Cnt), .din(Cout), .str(nHalt), .clk(CLK));  // open: data, sel, ld, clr
  Comparator #(.width(1), .mode("twosComplement")) comparator_2 (.a(Cout), .b(CoutS), .eq(_passed));  // open: gt, lt
  LED #(.active("true")) \u_测试完成  (.in(halt));
  Counter #(.width(10), .max('h3ff), .ongoal("wrap"), .trigger("rising"), .behavior("old")) counter_2 (
    .count(NEQ), .Q(counter_2_q), .clk(CLK), .clr(halt));  // open: load, D, carry, preset
  \模十可逆计数器输出函数  \u_模十可逆计数器输出函数_1  (.S3(S[0]), .S2(S[1]), .S1(S[2]), .Cout(Cout), .S0(S[3]), .Mode(Mode));
  Pull_Resistor #(.pull(0)) pull_resistor_1 (.node(_passed));
  not not_2 (NEQ, _passed);
  and and_1 (and_1_out, ~halt, NEQ);  // AND_Gate
  RAM #(.addrWidth(10), .dataWidth(5), .bus("separate"), .Select("high")) ram_2 (
    .addr(counter_2_q), .din({Mode, S}), .str(and_1_out), .clk(CLK));  // open: data, sel, ld, clr
  _7_Segment_Display #(.active("true")) u_7_segment_display_1 (
    .g(multiplexer_1_out[15]), .f(multiplexer_1_out[14]), .a(multiplexer_1_out[13]),
    .b(multiplexer_1_out[12]), .e(multiplexer_1_out_2[15]), .d(multiplexer_1_out_2[14]),
    .c(multiplexer_1_out_2[13]), .dp(multiplexer_1_out_2[12]));
  _7_Segment_Display #(.active("true")) u_7_segment_display_2 (
    .g(multiplexer_1_out[11]), .f(multiplexer_1_out[10]), .a(multiplexer_1_out[9]), .b(multiplexer_1_out[8]),
    .e(multiplexer_1_out_2[11]), .d(multiplexer_1_out_2[10]), .c(multiplexer_1_out_2[9]),
    .dp(multiplexer_1_out_2[8]));
  D_Flip_Flop #(.trigger("rising"), .Pre_Clr_Positions("LEGACY"), .NegatePresetClear("false"), .enable("true"), .NewFFLayout("false")) d_ff_1 (
    .clk(CLK), .D(NEQ), .Q(d_ff_1_q), .Qn(d_ff_1_qn), .en(d_ff_1_qn));  // open: preset, reset
  _7_Segment_Display #(.active("true")) u_7_segment_display_3 (
    .g(multiplexer_1_out[3]), .f(multiplexer_1_out[2]), .a(multiplexer_1_out[1]), .b(multiplexer_1_out[0]),
    .e(multiplexer_1_out_2[3]), .d(multiplexer_1_out_2[2]), .c(multiplexer_1_out_2[1]),
    .dp(multiplexer_1_out_2[0]));
  _7_Segment_Display #(.active("true")) u_7_segment_display_4 (
    .g(multiplexer_1_out[7]), .f(multiplexer_1_out[6]), .a(multiplexer_1_out[5]), .b(multiplexer_1_out[4]),
    .e(multiplexer_1_out_2[7]), .d(multiplexer_1_out_2[6]), .c(multiplexer_1_out_2[5]),
    .dp(multiplexer_1_out_2[4]));
  Multiplexer #(.select(1), .width(32), .disabled(0), .enable("true")) multiplexer_1 (
    .in0(32'h8a66ffee), .in1(32'h8a8cef44), .out({multiplexer_1_out_2, multiplexer_1_out}), .sel(d_ff_1_q),
    .en(halt));

  // Other names for the same wires on the sheet: Equal = _passed; Input[4:0] = {Mode, S}; tunnel[7:0] = Cnt

  // Notes on the sheet:
  //   测试节拍数
  //   contents of rom_1 (hex, n*v repeats v):
  //   0 1 2 3 4 5 6 7 8 9 a b c d e f 10 11 12 13 14 15 16 17 18 19 1a 1b 1c 1d 1e 1f 0 1 2 3 4 5 6 7 8 9
  //   a b c d e f 10 11 12 13 14 15 16 17 18 19 1a 1b 1c 1d 1e 1f 0 1 2 3 4 5 6 7 8 9 a b c d e f 10 11 12
  //   13 14 15 16 17 18 19 1a 1b 1c 1d 1e 1f 0 1 2 3 4 5 6 7 8 9 a b c d e f 10 11 12 13 14 15 16 17 18 19
  //   1a 1b 1c 1d 1e 1f 0 1 2 3 4 5 6 7 8 9 a b c d e f 10 11 12 13 14 15 16 17 18 19 1a 1b 1c 1d 1e 1f 0
  //   1 2 3 4 5 6 7 8 9 a b c d e f 10 11 12 13 14 15 16 17 18 19 1a 1b 1c 1d 1e 1f 0 1 2 3 4 5 6 7 8 9 a
  //   b c d e f 10 11 12 13 14 15 16 17 18 19 1a 1b 1c 1d 1e 1f 0 1 2 3 4 5 6 7 8 9 a b c d e f 10 11 12
  //   13 14 15 16 17 18 19 1a 1b 1c 1d 1e
  //   contents of rom_2 (hex, n*v repeats v):
  //   9*0 1 6*0 1
  //   错误记录X&Y
  //   存储器保存未通过的测试用例
  //   模十可逆计数器输出函数自动测试
  //   ctrl+K驱动时钟自动测试
endmodule

module \模十可逆计数器_可异步置位  (
  input  CLK,
  input  \使能 ,
  input  \异步置位控制 ,
  input  [3:0] \异步预置 ,
  input  \Mode_0正计数_1倒计数 ,
  output [3:0] \输出Q ,
  output \进位_借位 
);

  wire D0, D1, D2, D3, not_1_out, not_2_out, not_3_out, not_4_out, \模十可逆计数器激励函数_1_d0 , \模十可逆计数器激励函数_1_d1 ,
       \模十可逆计数器激励函数_1_d2 , \模十可逆计数器激励函数_1_d3 ;

  \模十可逆计数器激励函数  \u_模十可逆计数器激励函数_1  (
    .y3(\输出Q [3]), .y2(\输出Q [2]), .y1(\输出Q [1]), .y0(\输出Q [0]), .D3(\模十可逆计数器激励函数_1_d3 ),
    .Mode(\Mode_0正计数_1倒计数 ), .D2(\模十可逆计数器激励函数_1_d2 ), .D1(\模十可逆计数器激励函数_1_d1 ), .D0(\模十可逆计数器激励函数_1_d0 ));
  not not_1 (not_1_out, D3);
  not not_2 (not_2_out, D2);
  not not_3 (not_3_out, D1);
  not not_4 (not_4_out, D0);
  assign {D3, D2, D1, D0} = \异步置位控制  ? \异步预置  : 4'bz;  // Controlled_Buffer controlled_buffer_1
  D_Flip_Flop #(.trigger("rising"), .Pre_Clr_Positions("LEGACY"), .NegatePresetClear("false"), .enable("true"), .NewFFLayout("false")) u_D3 (
    .clk(CLK), .D(\模十可逆计数器激励函数_1_d3 ), .Q(\输出Q [3]), .preset(D3), .en(\使能 ), .reset(not_1_out));  // open: Qn
  D_Flip_Flop #(.trigger("rising"), .Pre_Clr_Positions("LEGACY"), .NegatePresetClear("false"), .enable("true"), .NewFFLayout("false")) u_D2 (
    .clk(CLK), .D(\模十可逆计数器激励函数_1_d2 ), .Q(\输出Q [2]), .preset(D2), .en(\使能 ), .reset(not_2_out));  // open: Qn
  D_Flip_Flop #(.trigger("rising"), .Pre_Clr_Positions("LEGACY"), .NegatePresetClear("false"), .enable("true"), .NewFFLayout("false")) u_D1 (
    .clk(CLK), .D(\模十可逆计数器激励函数_1_d1 ), .Q(\输出Q [1]), .preset(D1), .en(\使能 ), .reset(not_3_out));  // open: Qn
  D_Flip_Flop #(.trigger("rising"), .Pre_Clr_Positions("LEGACY"), .NegatePresetClear("false"), .enable("true"), .NewFFLayout("false")) u_D0 (
    .clk(CLK), .D(\模十可逆计数器激励函数_1_d0 ), .Q(\输出Q [0]), .preset(D0), .en(\使能 ), .reset(not_4_out));  // open: Qn
  // Probe on \输出Q 
  \模十可逆计数器输出函数  \u_模十可逆计数器输出函数_1  (
    .S3(\输出Q [3]), .S2(\输出Q [2]), .S1(\输出Q [1]), .Cout(\进位_借位 ), .S0(\输出Q [0]), .Mode(\Mode_0正计数_1倒计数 ));

  // Other names for the same wires on the sheet: Cout = \进位_借位 ; Din[3:0] = \异步预置 ; En = \使能 ;
  //   Mode = \Mode_0正计数_1倒计数 ; PreSet = \异步置位控制 ; Q[3:0] = \输出Q 

  // Notes on the sheet:
  //   友情提示：异步置位控制置位和复位端，D3~D0蓝线正常
  //   正计数到9，倒计数到0时输出为1
endmodule

module \模十可逆计数器测试电路  (
  output [7:0] Cnt,
  output En,
  output Count,
  output PreS,
  output [3:0] Din,
  output [3:0] Out,
  output Cout,
  output _passed,
  output halt
);

  wire and_1_out, and_2_out, CLK, d_ff_1_q, d_ff_1_qn, NEQ, nHalt;
  wire [4:0] OutputS;
  wire [9:0] counter_2_q;
  wire [15:0] multiplexer_1_out, multiplexer_1_out_2;

  Clock #(.highDuration(1), .lowDuration(1)) clock_1 (.out(CLK));
  Counter #(.width(8), .max('hff), .ongoal("wrap"), .trigger("rising"), .behavior("old")) counter_1 (
    .count(nHalt), .Q(Cnt), .clk(CLK));  // open: load, D, carry, clr, preset
  // Probe on Cnt
  // Probe on Cnt
  // Probe on 8'h3f
  not not_1 (nHalt, halt);
  Comparator #(.width(8), .mode("twosComplement")) comparator_1 (.a(Cnt), .b(8'h3f), .eq(halt));  // open: gt, lt
  ROM #(.addrWidth(8), .dataWidth(1), .Select("high")) rom_1 (.addr(Cnt), .data(En));
  ROM #(.addrWidth(8), .dataWidth(1), .Select("high")) rom_2 (.addr(Cnt), .data(Count));
  ROM #(.addrWidth(8), .dataWidth(1), .Select("high")) rom_3 (.addr(Cnt), .data(PreS));
  ROM #(.addrWidth(8), .dataWidth(4), .Select("high")) rom_4 (.addr(Cnt), .data(Din));
  ROM #(.addrWidth(8), .dataWidth(5), .Select("high")) rom_5 (.addr(Cnt), .data(OutputS));
  RAM #(.addrWidth(8), .dataWidth(5), .bus("separate"), .Select("low")) ram_1 (
    .addr(Cnt), .din({Cout, Out}), .str(nHalt), .clk(CLK));  // open: data, sel, ld, clr
  // Probe on Out
  \模十可逆计数器_可异步置位  \u_模十可逆计数器_可异步置位_1  (
    .CLK(CLK), .\使能 (En), .\输出Q (Out), .\异步置位控制 (PreS), .\异步预置 (Din), .\进位_借位 (Cout), .\Mode_0正计数_1倒计数 (Count));
  Comparator #(.width(5), .mode("twosComplement")) comparator_2 (
    .a({Cout, Out}), .b(OutputS), .eq(_passed));  // open: gt, lt
  LED #(.active("true")) \u_测试完成  (.in(halt));
  Counter #(.width(10), .max('h3ff), .ongoal("wrap"), .trigger("rising"), .behavior("old")) counter_2 (
    .count(NEQ), .Q(counter_2_q), .clk(CLK), .clr(halt));  // open: load, D, carry, preset
  Pull_Resistor #(.pull(0)) pull_resistor_1 (.node(_passed));
  not not_2 (NEQ, _passed);
  and and_1 (and_1_out, ~halt, NEQ);  // AND_Gate
  RAM #(.addrWidth(10), .dataWidth(5), .bus("separate"), .Select("high")) ram_2 (
    .addr(counter_2_q), .din({Cout, Out}), .str(and_1_out), .clk(CLK));  // open: data, sel, ld, clr
  and and_2 (and_2_out, NEQ, nHalt);
  _7_Segment_Display #(.active("true")) u_7_segment_display_1 (
    .g(multiplexer_1_out[11]), .f(multiplexer_1_out[10]), .a(multiplexer_1_out[9]), .b(multiplexer_1_out[8]),
    .e(multiplexer_1_out_2[11]), .d(multiplexer_1_out_2[10]), .c(multiplexer_1_out_2[9]),
    .dp(multiplexer_1_out_2[8]));
  _7_Segment_Display #(.active("true")) u_7_segment_display_2 (
    .g(multiplexer_1_out[15]), .f(multiplexer_1_out[14]), .a(multiplexer_1_out[13]),
    .b(multiplexer_1_out[12]), .e(multiplexer_1_out_2[15]), .d(multiplexer_1_out_2[14]),
    .c(multiplexer_1_out_2[13]), .dp(multiplexer_1_out_2[12]));
  _7_Segment_Display #(.active("true")) u_7_segment_display_3 (
    .g(multiplexer_1_out[3]), .f(multiplexer_1_out[2]), .a(multiplexer_1_out[1]), .b(multiplexer_1_out[0]),
    .e(multiplexer_1_out_2[3]), .d(multiplexer_1_out_2[2]), .c(multiplexer_1_out_2[1]),
    .dp(multiplexer_1_out_2[0]));
  _7_Segment_Display #(.active("true")) u_7_segment_display_4 (
    .g(multiplexer_1_out[7]), .f(multiplexer_1_out[6]), .a(multiplexer_1_out[5]), .b(multiplexer_1_out[4]),
    .e(multiplexer_1_out_2[7]), .d(multiplexer_1_out_2[6]), .c(multiplexer_1_out_2[5]),
    .dp(multiplexer_1_out_2[4]));
  D_Flip_Flop #(.trigger("rising"), .Pre_Clr_Positions("LEGACY"), .NegatePresetClear("false"), .enable("true"), .NewFFLayout("false")) d_ff_1 (
    .clk(CLK), .D(and_2_out), .Q(d_ff_1_q), .Qn(d_ff_1_qn), .en(d_ff_1_qn));  // open: preset, reset
  Multiplexer #(.select(1), .width(32), .disabled(0), .enable("true")) multiplexer_1 (
    .in0(32'h8a66ffee), .in1(32'h8a8cef44), .out({multiplexer_1_out_2, multiplexer_1_out}), .sel(d_ff_1_q),
    .en(halt));

  // Other names for the same wires on the sheet: Equal = _passed; Output[4:0] = {Cout, Out}; PreSet = PreS;
  //   tunnel[7:0] = Cnt

  // Notes on the sheet:
  //   测试节拍数
  //   contents of rom_1 (hex, n*v repeats v):
  //   16*0 128*1
  //   contents of rom_2 (hex, n*v repeats v):
  //   27*1
  //   contents of rom_3 (hex, n*v repeats v):
  //   16*1
  //   contents of rom_4 (hex, n*v repeats v):
  //   8 9 6 7 5 4 3 2 0 1 1 2 3 4 5 0 1
  //   contents of rom_5 (hex, n*v repeats v):
  //   8 9 6 7 5 4 3 2 10 1 1 2 3 4 5 10 10 9 8 7 6 5 4 3 2 1 10 19 0 1 2 3 4 5 6 7 8 19 0 1 2 3 4 5 6 7 8
  //   19 0 1 2 3 4 5 6 7 8 19 0 1 2 3 4
  //   错误记录X&Y
  //   存储器保存未通过的测试用例
  //   模十可逆计数器自动测试
  //   ctrl+K驱动时钟自动测试
endmodule

module \两位十进制可逆计数器  (
  input  CLK,
  input  \使能 ,
  input  \异步置位控制 ,
  input  [7:0] \异步预置 ,
  input  \Mode_0正计数_1倒计数 ,
  output [7:0] Q,
  output \进位_借位 
);

  wire and_1_out, \模十可逆计数器_可异步置位_1_进位_借位 , \模十可逆计数器_可异步置位_2_进位_借位 ;

  \模十可逆计数器_可异步置位  \u_模十可逆计数器_可异步置位_1  (
    .CLK(CLK), .\使能 (\使能 ), .\输出Q (Q[3:0]), .\异步置位控制 (\异步置位控制 ), .\异步预置 (\异步预置 [3:0]),
    .\进位_借位 (\模十可逆计数器_可异步置位_1_进位_借位 ), .\Mode_0正计数_1倒计数 (\Mode_0正计数_1倒计数 ));
  and and_1 (and_1_out, \使能 , \模十可逆计数器_可异步置位_1_进位_借位 );
  \模十可逆计数器_可异步置位  \u_模十可逆计数器_可异步置位_2  (
    .CLK(CLK), .\使能 (and_1_out), .\输出Q (Q[7:4]), .\异步置位控制 (\异步置位控制 ), .\异步预置 (\异步预置 [7:4]),
    .\进位_借位 (\模十可逆计数器_可异步置位_2_进位_借位 ), .\Mode_0正计数_1倒计数 (\Mode_0正计数_1倒计数 ));
  and and_2 (\进位_借位 , \模十可逆计数器_可异步置位_2_进位_借位 , \模十可逆计数器_可异步置位_1_进位_借位 );
  // Probe on Q

  // Other names for the same wires on the sheet: Cout = \进位_借位 ; Din[7:0] = \异步预置 ; Din0[3:0] = \异步预置 [3:0];
  //   Din1[3:0] = \异步预置 [7:4]; En = \使能 ; Mode = \Mode_0正计数_1倒计数 ; PreSet = \异步置位控制 

  // Notes on the sheet:
  //   正计数到9，倒计数到0时输出为1
endmodule

module \两位十进制可逆计数器测试电路  (
  output [7:0] Cnt,
  output En,
  output Count,
  output PreS,
  output [7:0] Din,
  output [7:0] Out,
  output Cout,
  output [8:0] Out_2,
  output _passed,
  output halt
);

  wire and_1_out, and_2_out, CLK, d_ff_1_q, d_ff_1_qn, NEQ, nHalt, not_3_out;
  wire [8:0] OutputS;
  wire [9:0] counter_2_q;
  wire [15:0] multiplexer_1_out, multiplexer_1_out_2;

  Clock #(.highDuration(1), .lowDuration(1)) clock_1 (.out(CLK));
  Counter #(.width(8), .max('hff), .ongoal("wrap"), .trigger("rising"), .behavior("old")) counter_1 (
    .count(nHalt), .Q(Cnt), .clk(CLK));  // open: load, D, carry, clr, preset
  // Probe on Cnt
  // Probe on Cnt
  // Probe on 8'h3f
  not not_1 (nHalt, halt);
  Comparator #(.width(8), .mode("twosComplement")) comparator_1 (.a(Cnt), .b(8'h3f), .eq(halt));  // open: gt, lt
  ROM #(.addrWidth(8), .dataWidth(1), .Select("high")) rom_1 (.addr(Cnt), .data(En));
  ROM #(.addrWidth(8), .dataWidth(1), .Select("high")) rom_2 (.addr(Cnt), .data(Count));
  ROM #(.addrWidth(8), .dataWidth(1), .Select("high")) rom_3 (.addr(Cnt), .data(PreS));
  ROM #(.addrWidth(8), .dataWidth(8), .Select("high")) rom_4 (.addr(Cnt), .data(Din));
  ROM #(.addrWidth(8), .dataWidth(9), .Select("high")) rom_5 (.addr(Cnt), .data(OutputS));
  RAM #(.addrWidth(8), .dataWidth(9), .bus("separate"), .Select("low")) ram_1 (
    .addr(Cnt), .din({Cout, Out}), .str(nHalt), .clk(CLK));  // open: data, sel, ld, clr
  // Probe on Out
  \两位十进制可逆计数器  \u_两位十进制可逆计数器_1  (
    .CLK(CLK), .\使能 (En), .Q(Out), .\异步置位控制 (PreS), .\异步预置 (Din), .\进位_借位 (Cout), .\Mode_0正计数_1倒计数 (Count));
  Comparator #(.width(9), .mode("unsigned")) comparator_2 (.a({Cout, Out}), .b(OutputS), .eq(_passed));  // open: gt, lt
  LED #(.active("true")) \u_测试完成  (.in(halt));
  Counter #(.width(10), .max('h3ff), .ongoal("wrap"), .trigger("rising"), .behavior("old")) counter_2 (
    .count(NEQ), .Q(counter_2_q), .clk(CLK), .clr(halt));  // open: load, D, carry, preset
  Pull_Resistor #(.pull(0)) pull_resistor_1 (.node(_passed));
  and and_1 (and_1_out, ~halt, NEQ);  // AND_Gate
  not not_2 (NEQ, _passed);
  RAM #(.addrWidth(10), .dataWidth(9), .bus("separate"), .Select("high")) ram_2 (
    .addr(counter_2_q), .din({Cout, Out}), .str(and_1_out), .clk(CLK));  // open: data, sel, ld, clr
  _7_Segment_Display #(.active("true")) u_7_segment_display_1 (
    .g(multiplexer_1_out[15]), .f(multiplexer_1_out[14]), .a(multiplexer_1_out[13]),
    .b(multiplexer_1_out[12]), .e(multiplexer_1_out_2[15]), .d(multiplexer_1_out_2[14]),
    .c(multiplexer_1_out_2[13]), .dp(multiplexer_1_out_2[12]));
  _7_Segment_Display #(.active("true")) u_7_segment_display_2 (
    .g(multiplexer_1_out[11]), .f(multiplexer_1_out[10]), .a(multiplexer_1_out[9]), .b(multiplexer_1_out[8]),
    .e(multiplexer_1_out_2[11]), .d(multiplexer_1_out_2[10]), .c(multiplexer_1_out_2[9]),
    .dp(multiplexer_1_out_2[8]));
  not not_3 (not_3_out, halt);
  and and_2 (and_2_out, not_3_out, NEQ);
  _7_Segment_Display #(.active("true")) u_7_segment_display_3 (
    .g(multiplexer_1_out[7]), .f(multiplexer_1_out[6]), .a(multiplexer_1_out[5]), .b(multiplexer_1_out[4]),
    .e(multiplexer_1_out_2[7]), .d(multiplexer_1_out_2[6]), .c(multiplexer_1_out_2[5]),
    .dp(multiplexer_1_out_2[4]));
  _7_Segment_Display #(.active("true")) u_7_segment_display_4 (
    .g(multiplexer_1_out[3]), .f(multiplexer_1_out[2]), .a(multiplexer_1_out[1]), .b(multiplexer_1_out[0]),
    .e(multiplexer_1_out_2[3]), .d(multiplexer_1_out_2[2]), .c(multiplexer_1_out_2[1]),
    .dp(multiplexer_1_out_2[0]));
  D_Flip_Flop #(.trigger("rising"), .Pre_Clr_Positions("LEGACY"), .NegatePresetClear("false"), .enable("true"), .NewFFLayout("false")) d_ff_1 (
    .clk(CLK), .D(and_2_out), .Q(d_ff_1_q), .Qn(d_ff_1_qn), .en(d_ff_1_qn));  // open: preset, reset
  Multiplexer #(.select(1), .width(32), .disabled(0), .enable("true")) multiplexer_1 (
    .in0(32'h8a66ffee), .in1(32'h8a8cef44), .out({multiplexer_1_out_2, multiplexer_1_out}), .sel(d_ff_1_q),
    .en(halt));

  assign Out_2 = {Cout, Out};

  // Other names for the same wires on the sheet: Equal = _passed; Output[8:0] = {Cout, Out}; PreSet = PreS;
  //   tunnel[7:0] = Cnt

  // Notes on the sheet:
  //   测试节拍数
  //   contents of rom_1 (hex, n*v repeats v):
  //   16*0 16*1 16*0 16*1 16*0 64*1
  //   contents of rom_2 (hex, n*v repeats v):
  //   32*1
  //   contents of rom_3 (hex, n*v repeats v):
  //   16*1 16*0 16*1
  //   contents of rom_4 (hex, n*v repeats v):
  //   4f 6f 22 35 21 34 47 76 23 83 14 56 31 40 53 13 12 11 10 f e d c b a 9 8 7 6 5 4 3 f4 f6 33 53 12 42
  //   74 67 32 38 41 65 13 4 35 94 4f 6f 33 35 21 24 47 76 23 83 14 56 31 40 53 13
  //   contents of rom_5 (hex, n*v repeats v):
  //   4f 6f 22 35 21 34 47 76 23 83 14 56 31 40 53 13 13 12 11 10 9 8 7 6 5 4 3 2 1 100 99 98 f4 f6 33 53
  //   12 42 74 67 32 38 41 65 13 4 35 94 94 95 96 97 98 199 0 1 2 3 4 5 6 7 8
  //   错误记录X&Y
  //   存储器保存未通过的测试用例
  //   两位十进制可逆计数器自动测试
  //   ctrl+K驱动时钟自动测试
endmodule

module \交通灯控制器激励函数  (
  input  y2,
  input  y1,
  input  y0,
  input  H,
  input  MR,
  input  SR,
  input  Online,
  input  T4,
  input  T3,
  input  T2,
  input  T1,
  output D2,
  output D1,
  output D0
);

  wire and_1_out, and_2_out, and_3_out, and_4_out, and_5_out, and_6_out, and_7_out, and_8_out, and_9_out,
       and_10_out, and_11_out, and_12_out, and_13_out, and_14_out, and_15_out, and_16_out, and_17_out,
       and_18_out, and_19_out, and_20_out, and_21_out, and_22_out, and_23_out, and_24_out, and_25_out,
       and_26_out, and_27_out, and_28_out, and_29_out, and_30_out, and_31_out, and_32_out, and_33_out,
       and_34_out, and_35_out, and_36_out, not_1_out, not_2_out, not_3_out, not_4_out, not_5_out, not_6_out,
       not_7_out, not_8_out, not_9_out, not_10_out, not_11_out, not_12_out, not_13_out, not_14_out,
       not_15_out, not_16_out, not_17_out, not_18_out, not_19_out, not_20_out, not_21_out, not_22_out,
       not_23_out, not_24_out, not_25_out, not_26_out, not_27_out, not_28_out, not_29_out, not_30_out,
       not_31_out, not_32_out, not_33_out, not_34_out, not_35_out, not_36_out, not_37_out, not_38_out,
       not_39_out, not_40_out, not_41_out, not_42_out, not_43_out, not_44_out, not_45_out, not_46_out,
       not_47_out, not_48_out, not_49_out, not_50_out, not_51_out, not_52_out, not_53_out, not_54_out,
       not_55_out, not_56_out, not_57_out, not_58_out, not_59_out, not_60_out, not_61_out, not_62_out,
       not_63_out, not_64_out, not_65_out, not_66_out, not_67_out, not_68_out, not_69_out, not_70_out,
       not_71_out, not_72_out, not_73_out, not_74_out, not_75_out, not_76_out, not_77_out, not_78_out,
       not_79_out, not_80_out, not_81_out, not_82_out, not_83_out, not_84_out, not_85_out, not_86_out,
       not_87_out, not_88_out, not_89_out, not_90_out, not_91_out, not_92_out, not_93_out;

  not not_1 (not_1_out, y2);
  not not_2 (not_2_out, y1);
  not not_3 (not_3_out, y0);
  not not_4 (not_4_out, MR);
  not not_5 (not_5_out, Online);
  not not_6 (not_6_out, y2);
  not not_7 (not_7_out, y1);
  not not_8 (not_8_out, y0);
  not not_9 (not_9_out, y2);
  not not_10 (not_10_out, y1);
  not not_11 (not_11_out, y2);
  not not_12 (not_12_out, y0);
  not not_13 (not_13_out, y2);
  not not_14 (not_14_out, y2);
  not not_15 (not_15_out, Online);
  not not_16 (not_16_out, y1);
  not not_17 (not_17_out, y0);
  not not_18 (not_18_out, y1);
  not not_19 (not_19_out, y1);
  not not_20 (not_20_out, MR);
  not not_21 (not_21_out, Online);
  not not_22 (not_22_out, y0);
  not not_23 (not_23_out, y1);
  not not_24 (not_24_out, y0);
  not not_25 (not_25_out, T3);
  not not_26 (not_26_out, y1);
  not not_27 (not_27_out, T4);
  not not_28 (not_28_out, y2);
  not not_29 (not_29_out, y1);
  not not_30 (not_30_out, y0);
  not not_31 (not_31_out, Online);
  not not_32 (not_32_out, y2);
  not not_33 (not_33_out, SR);
  not not_34 (not_34_out, Online);
  not not_35 (not_35_out, y1);
  not not_36 (not_36_out, Online);
  not not_37 (not_37_out, y2);
  not not_38 (not_38_out, y1);
  not not_39 (not_39_out, y0);
  not not_40 (not_40_out, H);
  not not_41 (not_41_out, Online);
  not not_42 (not_42_out, y2);
  not not_43 (not_43_out, H);
  not not_44 (not_44_out, SR);
  not not_45 (not_45_out, Online);
  not not_46 (not_46_out, y1);
  not not_47 (not_47_out, H);
  not not_48 (not_48_out, Online);
  and and_1 (and_1_out, not_1_out, not_2_out, not_3_out, not_4_out, SR, not_5_out);
  and and_2 (and_2_out, not_6_out, not_7_out, not_8_out, Online);
  and and_3 (and_3_out, not_9_out, not_10_out, y0, Online);
  and and_4 (and_4_out, not_11_out, y1, not_12_out, Online);
  and and_5 (and_5_out, not_13_out, y1, y0, Online);
  and and_6 (and_6_out, not_14_out, y1, y0, SR, not_15_out, T2);
  and and_7 (and_7_out, y2, not_16_out, not_17_out, T3);
  and and_8 (and_8_out, y2, not_18_out, y0, Online, T4);
  and and_9 (and_9_out, y2, not_19_out, y0, not_20_out, SR, not_21_out, T4);
  and and_10 (and_10_out, y2, y1, not_22_out, Online);
  and and_11 (and_11_out, y2, not_23_out, not_24_out, not_25_out);
  and and_12 (and_12_out, y2, not_26_out, y0, not_27_out);
  not not_49 (not_49_out, y2);
  not not_50 (not_50_out, y1);
  not not_51 (not_51_out, y0);
  not not_52 (not_52_out, y2);
  not not_53 (not_53_out, y1);
  not not_54 (not_54_out, y2);
  not not_55 (not_55_out, y1);
  not not_56 (not_56_out, Online);
  not not_57 (not_57_out, y2);
  not not_58 (not_58_out, y0);
  not not_59 (not_59_out, Online);
  not not_60 (not_60_out, y2);
  not not_61 (not_61_out, y0);
  not not_62 (not_62_out, y2);
  not not_63 (not_63_out, y1);
  not not_64 (not_64_out, y0);
  not not_65 (not_65_out, y0);
  not not_66 (not_66_out, Online);
  not not_67 (not_67_out, y2);
  not not_68 (not_68_out, y0);
  not not_69 (not_69_out, Online);
  not not_70 (not_70_out, T1);
  not not_71 (not_71_out, y2);
  not not_72 (not_72_out, Online);
  not not_73 (not_73_out, T2);
  not not_74 (not_74_out, y2);
  not not_75 (not_75_out, y1);
  not not_76 (not_76_out, Online);
  not not_77 (not_77_out, y2);
  not not_78 (not_78_out, y1);
  not not_79 (not_79_out, Online);
  not not_80 (not_80_out, T1);
  not not_81 (not_81_out, y2);
  not not_82 (not_82_out, y0);
  not not_83 (not_83_out, Online);
  not not_84 (not_84_out, y1);
  not not_85 (not_85_out, y0);
  not not_86 (not_86_out, y0);
  not not_87 (not_87_out, H);
  not not_88 (not_88_out, Online);
  not not_89 (not_89_out, y2);
  not not_90 (not_90_out, Online);
  not not_91 (not_91_out, T2);
  not not_92 (not_92_out, y1);
  not not_93 (not_93_out, T4);
  and and_13 (and_13_out, not_28_out, not_29_out, not_30_out, H, MR, not_31_out);
  and and_14 (and_14_out, not_49_out, not_50_out, not_51_out, Online);
  and and_15 (and_15_out, not_52_out, not_53_out, y0, Online);
  and and_16 (and_16_out, not_54_out, not_55_out, y0, not_56_out, T1);
  and and_17 (and_17_out, not_57_out, y1, not_58_out, not_59_out, T1);
  and and_18 (and_18_out, not_60_out, y1, not_61_out, Online);
  and and_19 (and_19_out, not_62_out, y1, y0, Online);
  and and_20 (and_20_out, not_32_out, y1, y0, H, MR, not_33_out, not_34_out, T2);
  and and_21 (and_21_out, y2, not_63_out, y0, Online, T4);
  and and_22 (and_22_out, y2, not_35_out, y0, H, MR, not_36_out, T4);
  and and_23 (and_23_out, y2, y1, not_64_out, Online);
  and and_24 (and_24_out, y2, y1, not_65_out, H, not_66_out);
  and and_25 (and_25_out, not_67_out, y1, not_68_out, not_69_out, not_70_out);
  and and_26 (and_26_out, not_71_out, y1, y0, not_72_out, not_73_out);
  and and_27 (and_27_out, not_37_out, not_38_out, not_39_out, not_40_out, MR, not_41_out);
  and and_28 (and_28_out, not_74_out, not_75_out, y0, not_76_out, T1);
  and and_29 (and_29_out, not_77_out, not_78_out, y0, not_79_out, not_80_out);
  and and_30 (and_30_out, not_81_out, y1, not_82_out, not_83_out, T1);
  and and_31 (and_31_out, not_42_out, y1, y0, not_43_out, MR, not_44_out, not_45_out, T2);
  and and_32 (and_32_out, y2, not_84_out, not_85_out, T3);
  and and_33 (and_33_out, y2, y1, not_86_out, not_87_out, not_88_out);
  and and_34 (and_34_out, y2, not_46_out, y0, not_47_out, MR, not_48_out, T4);
  and and_35 (and_35_out, not_89_out, y1, y0, not_90_out, not_91_out);
  and and_36 (and_36_out, y2, not_92_out, y0, not_93_out);
  or or_1 (D2, and_1_out, and_2_out, and_3_out, and_4_out, and_5_out, and_6_out, and_7_out, and_8_out, and_9_out, and_10_out, and_11_out, and_12_out);
  or or_2 (D1, and_13_out, and_14_out, and_15_out, and_16_out, and_17_out, and_18_out, and_19_out, and_20_out, and_21_out, and_22_out, and_23_out, and_24_out, and_25_out, and_26_out);
  or or_3 (D0, and_27_out, and_28_out, and_29_out, and_30_out, and_31_out, and_32_out, and_33_out, and_34_out, and_35_out, and_36_out);
endmodule

module \交通灯控制器激励函数测试电路  (
  output [7:0] Cnt,
  output [2:0] S,
  output [4:0] Tn,
  output [2:0] P,
  output [2:0] NS,
  output _passed,
  output halt
);

  wire and_1_out, CLK, d_ff_1_q, d_ff_1_qn, NEQ, nHalt;
  wire [2:0] NSs;
  wire [9:0] counter_2_q;
  wire [15:0] multiplexer_1_out, multiplexer_1_out_2;

  Clock #(.highDuration(1), .lowDuration(1)) clock_1 (.out(CLK));
  Counter #(.width(8), .max('hff), .ongoal("wrap"), .trigger("rising"), .behavior("old")) counter_1 (
    .count(nHalt), .Q(Cnt), .clk(CLK));  // open: load, D, carry, clr, preset
  // Probe on Cnt
  // Probe on Cnt
  // Probe on 8'h1b
  Comparator #(.width(8), .mode("twosComplement")) comparator_1 (.a(Cnt), .b(8'h1b), .eq(halt));  // open: gt, lt
  ROM #(.addrWidth(8), .dataWidth(3), .Select("high")) rom_1 (.addr(Cnt), .data(S));
  ROM #(.addrWidth(8), .dataWidth(5), .Select("high")) rom_2 (.addr(Cnt), .data(Tn));
  ROM #(.addrWidth(8), .dataWidth(3), .Select("high")) rom_3 (.addr(Cnt), .data(P));
  ROM #(.addrWidth(8), .dataWidth(3), .Select("high")) rom_4 (.addr(Cnt), .data(NSs));
  not not_1 (nHalt, halt);
  RAM #(.addrWidth(8), .dataWidth(3), .bus("separate"), .Select("low")) ram_1 (
    .addr(Cnt), .din(NS), .str(nHalt), .clk(CLK));  // open: data, sel, ld, clr
  Comparator #(.width(3), .mode("unsigned")) comparator_2 (.a(NS), .b(NSs), .eq(_passed));  // open: gt, lt
  LED #(.active("true")) \u_测试完成  (.in(halt));
  Counter #(.width(10), .max('h3ff), .ongoal("wrap"), .trigger("rising"), .behavior("old")) counter_2 (
    .count(NEQ), .Q(counter_2_q), .clk(CLK), .clr(halt));  // open: load, D, carry, preset
  Pull_Resistor #(.pull(0)) pull_resistor_1 (.node(_passed));
  and and_1 (and_1_out, ~halt, NEQ);  // AND_Gate
  \交通灯控制器激励函数  \u_交通灯控制器激励函数_1  (
    .y2(S[2]), .y1(S[1]), .y0(S[0]), .H(P[2]), .MR(P[1]), .SR(P[0]), .Online(Tn[4]), .T4(Tn[3]), .T3(Tn[2]),
    .T2(Tn[1]), .T1(Tn[0]), .D2(NS[2]), .D1(NS[1]), .D0(NS[0]));
  not not_2 (NEQ, _passed);
  RAM #(.addrWidth(10), .dataWidth(3), .bus("separate"), .Select("high")) ram_2 (
    .addr(counter_2_q), .din(NS), .str(and_1_out), .clk(CLK));  // open: data, sel, ld, clr
  _7_Segment_Display #(.active("true")) u_7_segment_display_1 (
    .g(multiplexer_1_out[11]), .f(multiplexer_1_out[10]), .a(multiplexer_1_out[9]), .b(multiplexer_1_out[8]),
    .e(multiplexer_1_out_2[11]), .d(multiplexer_1_out_2[10]), .c(multiplexer_1_out_2[9]),
    .dp(multiplexer_1_out_2[8]));
  _7_Segment_Display #(.active("true")) u_7_segment_display_2 (
    .g(multiplexer_1_out[15]), .f(multiplexer_1_out[14]), .a(multiplexer_1_out[13]),
    .b(multiplexer_1_out[12]), .e(multiplexer_1_out_2[15]), .d(multiplexer_1_out_2[14]),
    .c(multiplexer_1_out_2[13]), .dp(multiplexer_1_out_2[12]));
  D_Flip_Flop #(.trigger("rising"), .Pre_Clr_Positions("LEGACY"), .NegatePresetClear("false"), .enable("true"), .NewFFLayout("false")) d_ff_1 (
    .clk(CLK), .D(NEQ), .Q(d_ff_1_q), .Qn(d_ff_1_qn), .en(d_ff_1_qn));  // open: preset, reset
  _7_Segment_Display #(.active("true")) u_7_segment_display_3 (
    .g(multiplexer_1_out[3]), .f(multiplexer_1_out[2]), .a(multiplexer_1_out[1]), .b(multiplexer_1_out[0]),
    .e(multiplexer_1_out_2[3]), .d(multiplexer_1_out_2[2]), .c(multiplexer_1_out_2[1]),
    .dp(multiplexer_1_out_2[0]));
  _7_Segment_Display #(.active("true")) u_7_segment_display_4 (
    .g(multiplexer_1_out[7]), .f(multiplexer_1_out[6]), .a(multiplexer_1_out[5]), .b(multiplexer_1_out[4]),
    .e(multiplexer_1_out_2[7]), .d(multiplexer_1_out_2[6]), .c(multiplexer_1_out_2[5]),
    .dp(multiplexer_1_out_2[4]));
  Multiplexer #(.select(1), .width(32), .disabled(0), .enable("true")) multiplexer_1 (
    .in0(32'h8a66ffee), .in1(32'h8a8cef44), .out({multiplexer_1_out_2, multiplexer_1_out}), .sel(d_ff_1_q),
    .en(halt));

  // Other names for the same wires on the sheet: Equal = _passed; tunnel[7:0] = Cnt

  // Notes on the sheet:
  //   测试节拍数
  //   contents of rom_1 (hex, n*v repeats v):
  //   4*0 5*1 5*2 3 3 4 4 4 5 5 4*6 7 7
  //   contents of rom_2 (hex, n*v repeats v):
  //   3 1a 12 14 4*1 0 4*1 0 2 8 4 4 8 8 0 16 16 16 0 2 4
  //   contents of rom_3 (hex, n*v repeats v):
  //   2 1 2 0 0 1 2 3 3 0 1 2 3 7 7 7 2 5 7 7 7 2 3 4*7
  //   contents of rom_4 (hex, n*v repeats v):
  //   1 6 6 6 4*3 1 4*3 2 4 3 5 5 4 2 5 6 6 6 2
  //   错误记录X&Y
  //   存储器保存未通过的测试用例
  //   红绿灯状态机自动测试
  //   ctrl+K驱动时钟自动测试
endmodule

module \交通灯控制器输出函数  (
  input  y2,
  input  y1,
  input  y0,
  output R1,
  output Y1_2,
  output G1,
  output R2,
  output Y2_2,
  output G2,
  output PASS0,
  output PASS1,
  output PASS2,
  output pass3
);

  wire and_2_out, and_3_out, and_4_out, and_5_out, and_6_out, and_7_out, and_8_out, and_9_out, and_10_out,
       and_13_out, and_14_out, not_1_out, not_2_out, not_3_out, not_4_out, not_5_out, not_6_out, not_7_out,
       not_8_out, not_9_out, not_10_out, not_11_out, not_12_out, not_13_out, not_14_out, not_15_out,
       not_16_out, not_17_out, not_18_out, not_19_out;

  not not_1 (not_1_out, y1);
  not not_2 (not_2_out, y2);
  not not_3 (not_3_out, y1);
  not not_4 (not_4_out, y0);
  not not_5 (not_5_out, y2);
  not not_6 (not_6_out, y1);
  not not_7 (not_7_out, y0);
  not not_8 (not_8_out, y2);
  not not_9 (not_9_out, y2);
  not not_10 (not_10_out, y1);
  not not_11 (not_11_out, y0);
  not not_12 (not_12_out, y1);
  not not_13 (not_13_out, y0);
  not not_14 (not_14_out, y2);
  not not_15 (not_15_out, y1);
  not not_16 (not_16_out, y0);
  not not_17 (not_17_out, y2);
  not not_18 (not_18_out, y2);
  not not_19 (not_19_out, y1);
  and and_1 (pass3, y2, y1);
  and and_2 (and_2_out, y2, not_1_out);
  and and_3 (and_3_out, y2, y0);
  and and_4 (and_4_out, not_2_out, not_3_out, not_4_out);
  and and_5 (and_5_out, y1, y0);
  and and_6 (and_6_out, not_5_out, not_6_out, y0);
  and and_7 (and_7_out, y1, not_7_out);
  and and_8 (and_8_out, not_8_out, y0);
  and and_9 (and_9_out, not_9_out, not_10_out, not_11_out);
  and and_10 (and_10_out, y2, y0);
  and and_11 (G2, y2, not_12_out, not_13_out);
  and and_12 (PASS0, not_14_out, not_15_out, not_16_out);
  and and_13 (and_13_out, not_17_out, y0);
  and and_14 (and_14_out, not_18_out, y1);
  and and_15 (PASS2, y2, not_19_out);
  or or_1 (R1, and_2_out, and_3_out);
  or or_2 (Y1_2, and_4_out, and_5_out);
  or or_3 (G1, and_6_out, and_7_out);
  or or_4 (R2, and_8_out, y1);
  or or_5 (Y2_2, and_9_out, and_10_out);
  or or_6 (PASS1, and_13_out, and_14_out);
endmodule

module \交通灯控制器输出函数测试电路  (
  output [7:0] Cnt,
  output [2:0] S,
  output [9:0] Cout,
  output _passed,
  output halt
);

  wire and_1_out, CLK, d_ff_1_q, d_ff_1_qn, NEQ, nHalt;
  wire [9:0] counter_2_q, CoutS;
  wire [15:0] multiplexer_1_out, multiplexer_1_out_2;

  Clock #(.highDuration(1), .lowDuration(1)) clock_1 (.out(CLK));
  Counter #(.width(8), .max('hff), .ongoal("wrap"), .trigger("rising"), .behavior("old")) counter_1 (
    .count(nHalt), .Q(Cnt), .clk(CLK));  // open: load, D, carry, clr, preset
  // Probe on Cnt
  // Probe on Cnt
  // Probe on 8'h7
  Comparator #(.width(8), .mode("twosComplement")) comparator_1 (.a(Cnt), .b(8'h7), .eq(halt));  // open: gt, lt
  ROM #(.addrWidth(8), .dataWidth(3), .Select("high")) rom_1 (.addr(Cnt), .data(S));
  ROM #(.addrWidth(8), .dataWidth(10), .Select("high")) rom_2 (.addr(Cnt), .data(CoutS));
  not not_1 (nHalt, halt);
  RAM #(.addrWidth(8), .dataWidth(10), .bus("separate"), .Select("high")) ram_1 (
    .addr(Cnt), .din(Cout), .str(nHalt), .clk(CLK));  // open: data, sel, ld, clr
  LED #(.active("true")) \u_测试完成  (.in(halt));
  Counter #(.width(10), .max('h3ff), .ongoal("wrap"), .trigger("rising"), .behavior("old")) counter_2 (
    .count(NEQ), .Q(counter_2_q), .clk(CLK), .clr(halt));  // open: load, D, carry, preset
  Pull_Resistor #(.pull(0)) pull_resistor_1 (.node(_passed));
  Comparator #(.width(10), .mode("unsigned")) comparator_2 (.a(Cout), .b(CoutS), .eq(_passed));  // open: gt, lt
  and and_1 (and_1_out, ~halt, NEQ);  // AND_Gate
  \交通灯控制器输出函数  \u_交通灯控制器输出函数_1  (
    .y2(S[2]), .R1(Cout[0]), .y1(S[1]), .y0(S[0]), .Y1_2(Cout[1]), .G1(Cout[2]), .R2(Cout[3]),
    .Y2_2(Cout[4]), .G2(Cout[5]), .PASS0(Cout[6]), .PASS1(Cout[7]), .PASS2(Cout[8]), .pass3(Cout[9]));
  not not_2 (NEQ, _passed);
  RAM #(.addrWidth(10), .dataWidth(3), .bus("separate"), .Select("high")) ram_2 (
    .addr(counter_2_q), .din(S), .str(and_1_out), .clk(CLK));  // open: data, sel, ld, clr
  _7_Segment_Display #(.active("true")) u_7_segment_display_1 (
    .g(multiplexer_1_out[15]), .f(multiplexer_1_out[14]), .a(multiplexer_1_out[13]),
    .b(multiplexer_1_out[12]), .e(multiplexer_1_out_2[15]), .d(multiplexer_1_out_2[14]),
    .c(multiplexer_1_out_2[13]), .dp(multiplexer_1_out_2[12]));
  _7_Segment_Display #(.active("true")) u_7_segment_display_2 (
    .g(multiplexer_1_out[11]), .f(multiplexer_1_out[10]), .a(multiplexer_1_out[9]), .b(multiplexer_1_out[8]),
    .e(multiplexer_1_out_2[11]), .d(multiplexer_1_out_2[10]), .c(multiplexer_1_out_2[9]),
    .dp(multiplexer_1_out_2[8]));
  D_Flip_Flop #(.trigger("rising"), .Pre_Clr_Positions("LEGACY"), .NegatePresetClear("false"), .enable("true"), .NewFFLayout("false")) d_ff_1 (
    .clk(CLK), .D(NEQ), .Q(d_ff_1_q), .Qn(d_ff_1_qn), .en(d_ff_1_qn));  // open: preset, reset
  _7_Segment_Display #(.active("true")) u_7_segment_display_3 (
    .g(multiplexer_1_out[3]), .f(multiplexer_1_out[2]), .a(multiplexer_1_out[1]), .b(multiplexer_1_out[0]),
    .e(multiplexer_1_out_2[3]), .d(multiplexer_1_out_2[2]), .c(multiplexer_1_out_2[1]),
    .dp(multiplexer_1_out_2[0]));
  _7_Segment_Display #(.active("true")) u_7_segment_display_4 (
    .g(multiplexer_1_out[7]), .f(multiplexer_1_out[6]), .a(multiplexer_1_out[5]), .b(multiplexer_1_out[4]),
    .e(multiplexer_1_out_2[7]), .d(multiplexer_1_out_2[6]), .c(multiplexer_1_out_2[5]),
    .dp(multiplexer_1_out_2[4]));
  Multiplexer #(.select(1), .width(32), .disabled(0), .enable("true")) multiplexer_1 (
    .in0(32'h8a66ffee), .in1(32'h8a8cef44), .out({multiplexer_1_out_2, multiplexer_1_out}), .sel(d_ff_1_q),
    .en(halt));

  // Other names for the same wires on the sheet: Equal = _passed; tunnel[7:0] = Cnt

  // Notes on the sheet:
  //   测试节拍数
  //   contents of rom_1 (hex, n*v repeats v):
  //   0 1 2 3 4 5 6 7
  //   contents of rom_2 (hex, n*v repeats v):
  //   52 8c 8c 8a 121 111 20c 21b
  //   错误记录X&Y
  //   存储器保存未通过的测试用例
  //   红绿灯状态输出函数自动测试
  //   ctrl+K驱动时钟自动测试
endmodule

module \交通灯控制系统  (
  input  in_1,
  input  in_2,
  input  in_3,
  input  online,
  output R1,
  output Y1,
  output [2:0] Status,
  output G1,
  output R2,
  output Y2,
  output [7:0] Timer,
  output G2
);

  wire CLK, or_1_out, PASS0, PASS1, PASS2, PASS3, T1, T2, T3, T4, T5, T6, Y1c, Y2c;
  wire [2:0] S1B, S2B, \交通灯控制器激励函数_1_d0 ;
  wire [3:0] S1T, S2T;
  wire [7:0] counter_1_q, \n8位2路选择器_1_out , \n8位2路选择器_2_out , \n8位2路选择器_3_out , Timer1, Timer2;

  LED #(.active("true")) led_1 (.in(R1));
  LED #(.active("true")) led_2 (.in(Y1c));
  LED #(.active("true")) led_3 (.in(G1));
  Register #(.width(3), .trigger("rising"), .Select("low")) \u_状态  (
    .D(\交通灯控制器激励函数_1_d0 ), .Q(Status), .clk(CLK));  // open: en, clr
  _7_Segment_Display #(.active("true")) u_7_segment_display_1 (
    .g(S2T[0]), .f(S2T[1]), .a(S2T[2]), .b(S2T[3]), .e(S2B[0]), .d(S2B[1]), .c(S2B[2]));  // open: dp
  _7_Segment_Display #(.active("true")) u_7_segment_display_2 (
    .g(S1T[0]), .f(S1T[1]), .a(S1T[2]), .b(S1T[3]), .e(S1B[0]), .d(S1B[1]), .c(S1B[2]));  // open: dp
  or or_1 (or_1_out, PASS3, PASS0, T5, T4);
  \_8位2路选择器  \u_8位2路选择器_1  (.X(8'h15), .Sel(in_1), .Y(8'h30), .Out(\n8位2路选择器_1_out ));
  LED #(.active("true")) led_4 (.in(R2));
  LED #(.active("true")) led_5 (.in(Y2c));
  LED #(.active("true")) led_6 (.in(G2));
  \交通灯控制器输出函数  \u_交通灯控制器输出函数_1  (
    .y2(Status[2]), .R1(R1), .y1(Status[1]), .y0(Status[0]), .Y1_2(Y1), .G1(G1), .R2(R2), .Y2_2(Y2), .G2(G2),
    .PASS0(PASS0), .PASS1(PASS1), .PASS2(PASS2), .pass3(PASS3));
  \两位十进制可逆计数器  \u_两位十进制可逆计数器_1  (
    .CLK(CLK), .\使能 (PASS1), .Q(Timer1), .\异步置位控制 (or_1_out), .\异步预置 (\n8位2路选择器_1_out ),
    .\Mode_0正计数_1倒计数 (1'b1));  // open: 进位_借位
  \_8位无符号比较器  \u_8位无符号比较器_1  (.X(Timer1), .Y(8'h4), .Equal(T1));  // open: Great, Less
  \_8位无符号比较器  \u_8位无符号比较器_2  (.X(Timer1), .Y(8'h1), .Equal(T2));  // open: Great, Less
  \_8位无符号比较器  \u_8位无符号比较器_3  (.X(Timer1), .Y({8{1'b0}}), .Equal(T5));  // open: Great, Less
  \交通灯控制器激励函数  \u_交通灯控制器激励函数_1  (
    .y2(Status[2]), .y1(Status[1]), .y0(Status[0]), .H(in_1), .MR(in_2), .SR(in_3), .Online(online), .T4(T4),
    .T3(T3), .T2(T2), .T1(T1), .D2(\交通灯控制器激励函数_1_d0 [2]), .D1(\交通灯控制器激励函数_1_d0 [1]), .D0(\交通灯控制器激励函数_1_d0 [0]));
  and and_1 (Y1c, Y1, CLK);
  and and_2 (Y2c, Y2, CLK);
  \_8位2路选择器  \u_8位2路选择器_2  (.X(\n8位2路选择器_3_out ), .Sel(PASS2), .Y(Timer2), .Out(\n8位2路选择器_2_out ));
  \_8位2路选择器  \u_8位2路选择器_3  (.X(Timer1), .Sel(PASS0), .Y({8{1'b0}}), .Out(\n8位2路选择器_3_out ));
  Clock #(.highDuration(1), .lowDuration(1)) clock_1 (.out(CLK));
  Counter #(.width(8), .max('hff), .ongoal("wrap"), .trigger("rising"), .behavior("new")) counter_1 (
    .Q(counter_1_q), .clk(CLK));  // open: load, D, count, carry, clr, preset, down
  \_8位2路选择器  \u_8位2路选择器_4  (.X(\n8位2路选择器_2_out ), .Sel(PASS3), .Y(8'h99), .Out(Timer));
  \两位十进制可逆计数器  \u_两位十进制可逆计数器_2  (
    .CLK(CLK), .\使能 (PASS2), .Q(Timer2), .\异步置位控制 (T6), .\异步预置 (8'h15), .\Mode_0正计数_1倒计数 (1'b1));  // open: 进位_借位
  // Probe on counter_1_q
  \_8位无符号比较器  \u_8位无符号比较器_4  (.X(Timer2), .Y(8'h4), .Equal(T3));  // open: Great, Less
  \_8位无符号比较器  \u_8位无符号比较器_5  (.X(Timer2), .Y(8'h1), .Equal(T4));  // open: Great, Less
  \_8位无符号比较器  \u_8位无符号比较器_6  (.X(Timer2), .Y({8{1'b0}}), .Equal(T6));  // open: Great, Less
  \七段显示译码器  \u_七段显示译码器_1  (
    .X3(Timer[7]), .X2(Timer[6]), .Seg_1(S2T[0]), .X1(Timer[5]), .X0(Timer[4]), .Seg_2(S2T[1]),
    .Seg_3(S2T[2]), .Seg_4(S2T[3]), .Seg_5(S2B[0]), .Seg_6(S2B[1]), .Seg_7(S2B[2]));
  \七段显示译码器  \u_七段显示译码器_2  (
    .X3(Timer[3]), .X2(Timer[2]), .Seg_1(S1T[0]), .X1(Timer[1]), .X0(Timer[0]), .Seg_2(S1T[1]),
    .Seg_3(S1T[2]), .Seg_4(S1T[3]), .Seg_5(S1B[0]), .Seg_6(S1B[1]), .Seg_7(S1B[2]));

  // Other names for the same wires on the sheet: H = in_1; MR = in_2; SR = in_3

  // Notes on the sheet:
  //   主道红绿灯
  //   主干道通行倒计时
  //   倒计时显示
  //   辅道红绿灯
  //   状态机现态
  //   当前倒计时
  //   引脚区，用于EduCoder测试
  //   倒计时选择模块
  //   次干道通行倒计时
  //   时钟计数
endmodule

module \交通灯测试  (
  output [7:0] Cnt,
  output [2:0] Status,
  output [7:0] Timer,
  output [8:0] RYG1,
  output [8:0] RYG2,
  output _passed,
  output halt
);

  wire and_1_out, CLK, comparator_2_eq, comparator_3_eq, comparator_4_eq, d_ff_1_q, d_ff_1_qn, NEQ, nHalt;
  wire [2:0] StatusS;
  wire [3:0] S;
  wire [5:0] RYGOutputS;
  wire [7:0] TimerS;
  wire [9:0] counter_2_q;
  wire [15:0] multiplexer_1_out, multiplexer_1_out_2;

  Clock #(.highDuration(1), .lowDuration(1)) clock_1 (.out(CLK));
  Counter #(.width(8), .max('hff), .ongoal("wrap"), .trigger("rising"), .behavior("old")) counter_1 (
    .count(nHalt), .Q(Cnt), .clk(CLK));  // open: load, D, carry, clr, preset
  // Probe on Cnt
  // Probe on Cnt
  // Probe on 8'hd1
  not not_1 (nHalt, halt);
  Comparator #(.width(8), .mode("twosComplement")) comparator_1 (.a(Cnt), .b(8'hd1), .eq(halt));  // open: gt, lt
  ROM #(.addrWidth(8), .dataWidth(4), .Select("high")) rom_1 (.addr(Cnt), .data(S));
  ROM #(.addrWidth(8), .dataWidth(6), .Select("high")) rom_2 (.addr(Cnt), .data(RYGOutputS));
  ROM #(.addrWidth(8), .dataWidth(3), .Select("high")) rom_3 (.addr(Cnt), .data(StatusS));
  ROM #(.addrWidth(8), .dataWidth(8), .Select("high")) rom_4 (.addr(Cnt), .data(TimerS));
  RAM #(.addrWidth(8), .dataWidth(6), .bus("separate"), .Select("high")) ram_1 (
    .addr(Cnt), .din({RYG2[0], RYG2[4], RYG2[8], RYG1[0], RYG1[4], RYG1[8]}), .str(nHalt), .clk(CLK));  // open: data, sel, ld, clr
  \交通灯控制系统  \u_交通灯控制系统_1  (
    .R1(RYG1[8]), .Y1(RYG1[4]), .in_1(S[0]), .Status(Status), .G1(RYG1[0]), .in_2(S[1]), .R2(RYG2[8]),
    .Y2(RYG2[4]), .in_3(S[2]), .Timer(Timer), .G2(RYG2[0]), .online(S[3]));
  Comparator #(.width(6), .mode("twosComplement")) comparator_2 (
    .a({RYG2[0], RYG2[4], RYG2[8], RYG1[0], RYG1[4], RYG1[8]}), .b(RYGOutputS), .eq(comparator_2_eq));  // open: gt, lt
  Comparator #(.width(3), .mode("twosComplement")) comparator_3 (
    .a(Status), .b(StatusS), .eq(comparator_3_eq));  // open: gt, lt
  Comparator #(.width(8), .mode("twosComplement")) comparator_4 (
    .a(Timer), .b(TimerS), .eq(comparator_4_eq));  // open: gt, lt
  LED #(.active("true")) \u_测试完成  (.in(halt));
  Counter #(.width(10), .max('h3ff), .ongoal("wrap"), .trigger("rising"), .behavior("old")) counter_2 (
    .count(NEQ), .Q(counter_2_q), .clk(CLK), .clr(halt));  // open: load, D, carry, preset
  Pull_Resistor #(.pull(0)) pull_resistor_1 (.node(comparator_2_eq));
  Pull_Resistor #(.pull(0)) pull_resistor_2 (.node(comparator_3_eq));
  Pull_Resistor #(.pull(0)) pull_resistor_3 (.node(comparator_4_eq));
  and and_1 (and_1_out, ~halt, NEQ);  // AND_Gate
  and and_2 (_passed, comparator_2_eq, comparator_3_eq, comparator_4_eq);
  RAM #(.addrWidth(10), .dataWidth(4), .bus("separate"), .Select("high")) ram_2 (
    .addr(counter_2_q), .din(S), .str(and_1_out), .clk(CLK));  // open: data, sel, ld, clr
  RAM #(.addrWidth(8), .dataWidth(3), .bus("separate"), .Select("high")) ram_3 (
    .addr(Cnt), .din(Status), .str(nHalt), .clk(CLK));  // open: data, sel, ld, clr
  _7_Segment_Display #(.active("true")) u_7_segment_display_1 (
    .g(multiplexer_1_out[15]), .f(multiplexer_1_out[14]), .a(multiplexer_1_out[13]),
    .b(multiplexer_1_out[12]), .e(multiplexer_1_out_2[15]), .d(multiplexer_1_out_2[14]),
    .c(multiplexer_1_out_2[13]), .dp(multiplexer_1_out_2[12]));
  _7_Segment_Display #(.active("true")) u_7_segment_display_2 (
    .g(multiplexer_1_out[11]), .f(multiplexer_1_out[10]), .a(multiplexer_1_out[9]), .b(multiplexer_1_out[8]),
    .e(multiplexer_1_out_2[11]), .d(multiplexer_1_out_2[10]), .c(multiplexer_1_out_2[9]),
    .dp(multiplexer_1_out_2[8]));
  D_Flip_Flop #(.trigger("falling"), .Pre_Clr_Positions("LEGACY"), .NegatePresetClear("false"), .enable("true"), .NewFFLayout("false")) d_ff_1 (
    .clk(CLK), .D(NEQ), .Q(d_ff_1_q), .Qn(d_ff_1_qn), .en(d_ff_1_qn));  // open: preset, reset
  not not_2 (NEQ, _passed);
  _7_Segment_Display #(.active("true")) u_7_segment_display_3 (
    .g(multiplexer_1_out[7]), .f(multiplexer_1_out[6]), .a(multiplexer_1_out[5]), .b(multiplexer_1_out[4]),
    .e(multiplexer_1_out_2[7]), .d(multiplexer_1_out_2[6]), .c(multiplexer_1_out_2[5]),
    .dp(multiplexer_1_out_2[4]));
  _7_Segment_Display #(.active("true")) u_7_segment_display_4 (
    .g(multiplexer_1_out[3]), .f(multiplexer_1_out[2]), .a(multiplexer_1_out[1]), .b(multiplexer_1_out[0]),
    .e(multiplexer_1_out_2[3]), .d(multiplexer_1_out_2[2]), .c(multiplexer_1_out_2[1]),
    .dp(multiplexer_1_out_2[0]));
  Multiplexer #(.select(1), .width(32), .disabled(0), .enable("true")) multiplexer_1 (
    .in0(32'h8a66ffee), .in1(32'h8a8cef44), .out({multiplexer_1_out_2, multiplexer_1_out}), .sel(d_ff_1_q),
    .en(halt));
  RAM #(.addrWidth(8), .dataWidth(8), .bus("separate"), .Select("high")) ram_4 (
    .addr(Cnt), .din(Timer), .str(nHalt), .clk(CLK));  // open: data, sel, ld, clr

  assign {RYG1[7:5], RYG1[3:1]} = {6{1'b0}};
  assign {RYG2[7:5], RYG2[3:1]} = {6{1'b0}};

  // Other names for the same wires on the sheet: Equal = _passed; G1 = RYG1[0];
  //   RYGOutput[5:0] = {RYG2[0], RYG2[4], RYG2[8], RYG1[0], RYG1[4], RYG1[8]}; Y1 = RYG1[4]; R1 = RYG1[8];
  //   G2 = RYG2[0]; Y2 = RYG2[4]; R2 = RYG2[8]; tunnel[7:0] = Cnt

  // Notes on the sheet:
  //   测试节拍数
  //   contents of rom_1 (hex, n*v repeats v):
  //   0 0 0 21*2 30*6 60*7 13*0 21*4 15*c 10*4 5*e 21*6
  //   contents of rom_2 (hex, n*v repeats v):
  //   4*12 12*c a a a 12*c a a a 12*21 11 11 11 12*c a a a 12*21 11 11 11 27*c a a a 12*21 11 11 11 4*12
  //   12*21 11 11 11 12*21 11 11 11 33*c a a a 12*21 11 11 11 12
  //   contents of rom_3 (hex, n*v repeats v):
  //   4*0 12*1 3 3 3 12*1 3 3 3 12*4 5 5 5 12*1 3 3 3 12*4 5 5 5 27*2 3 3 3 12*4 5 5 5 4*0 12*4 5 5 5 12*4
  //   5 5 5 6*6 10*1 5*6 12*1 3 3 3 12*4 5 5 5
  //   contents of rom_4 (hex, n*v repeats v):
  //   4*0 15 14 13 12 11 10 9 8 7 6 5 4 3 2 1 15 14 13 12 11 10 9 8 7 6 5 4 3 2 1 15 14 13 12 11 10 9 8 7
  //   6 5 4 3 2 1 15 14 13 12 11 10 9 8 7 6 5 4 3 2 1 15 14 13 12 11 10 9 8 7 6 5 4 3 2 1 30 29 28 27 26
  //   25 24 23 22 21 20 19 18 17 16 15 14 13 12 11 10 9 8 7 6 5 4 3 2 1 15 14 13 12 11 10 9 8 7 6 5 4 3 2
  //   1 4*0 15 14 13 12 11 10 9 8 7 6 5 4 3 2 1 15 14 13 12 11 10 9 8 7 6 5 4 3 2 1 6*99 15 14 13 12 11 10
  //   9 8 7 6 5*99 15 14 13 12 11 10 9 8 7 6 5 4 3 2 1 15 14 13 12 11 10 9 8 7 6 5 4 3 2 1
  //   错误记录X&Y
  //   存储器保存未通过的测试用例
  //   交通灯自动测试
  //   ctrl+K驱动时钟自动测试
endmodule
